// Logisim project Design of a 16-bit ALU IC..circ as structural Verilog
module _16_bit_register_file (
  input  [15:0] Write_Data,
  input  Write_enabler,
  input  [3:0] RS_Selector,
  input  [3:0] RT_Selector,
  input  [3:0] RD_Selector,
  input  Register_CLOCK,
  input  Register_CLEAR,
  output [15:0] Data_1_Out,
  output [15:0] Data_2_Out
);

  wire and_1_out, and_2_out, and_3_out, and_4_out, and_5_out, and_6_out, and_7_out, and_8_out, and_9_out,
       and_10_out, and_11_out, and_12_out, and_13_out, and_14_out, and_15_out, and_16_out, decoder_1_out0,
       decoder_1_out1, decoder_1_out2, decoder_1_out3, decoder_1_out4, decoder_1_out5, decoder_1_out6,
       decoder_1_out7, decoder_1_out8, decoder_1_out9, decoder_1_out10, decoder_1_out11, decoder_1_out12,
       decoder_1_out13, decoder_1_out14, decoder_1_out15;
  wire [15:0] s0_q, s1_q, s2_q, s3_q, s4_q, s5_q, s6_q, s7_q, s8_q, s9_q, s10_q, s11_q, s12_q, s13_q, s14_q,
       s15_q;

  Decoder #(.select(4), .enable("false")) decoder_1 (
    .out0(decoder_1_out0), .out1(decoder_1_out1), .out2(decoder_1_out2), .out3(decoder_1_out3),
    .out4(decoder_1_out4), .out5(decoder_1_out5), .out6(decoder_1_out6), .out7(decoder_1_out7),
    .out8(decoder_1_out8), .out9(decoder_1_out9), .out10(decoder_1_out10), .out11(decoder_1_out11),
    .out12(decoder_1_out12), .out13(decoder_1_out13), .out14(decoder_1_out14), .out15(decoder_1_out15),
    .sel(RD_Selector));
  and and_1 (and_1_out, decoder_1_out0, Write_enabler);
  and and_2 (and_2_out, decoder_1_out1, Write_enabler);
  and and_3 (and_3_out, decoder_1_out2, Write_enabler);
  and and_4 (and_4_out, decoder_1_out3, Write_enabler);
  and and_5 (and_5_out, decoder_1_out4, Write_enabler);
  and and_6 (and_6_out, decoder_1_out5, Write_enabler);
  and and_7 (and_7_out, decoder_1_out6, Write_enabler);
  and and_8 (and_8_out, decoder_1_out7, Write_enabler);
  and and_9 (and_9_out, decoder_1_out8, Write_enabler);
  and and_10 (and_10_out, decoder_1_out9, Write_enabler);
  and and_11 (and_11_out, decoder_1_out10, Write_enabler);
  and and_12 (and_12_out, decoder_1_out11, Write_enabler);
  and and_13 (and_13_out, decoder_1_out12, Write_enabler);
  and and_14 (and_14_out, decoder_1_out13, Write_enabler);
  and and_15 (and_15_out, decoder_1_out14, Write_enabler);
  and and_16 (and_16_out, decoder_1_out15, Write_enabler);
  Register #(.width(16)) s0 (.D(Write_Data), .en(and_1_out), .Q(s0_q), .clk(Register_CLOCK), .clr(Register_CLEAR));
  Register #(.width(16)) s1 (.D(Write_Data), .en(and_2_out), .Q(s1_q), .clk(Register_CLOCK), .clr(Register_CLEAR));
  Register #(.width(16)) s2 (.D(Write_Data), .en(and_3_out), .Q(s2_q), .clk(Register_CLOCK), .clr(Register_CLEAR));
  Register #(.width(16)) s3 (.D(Write_Data), .en(and_4_out), .Q(s3_q), .clk(Register_CLOCK), .clr(Register_CLEAR));
  Register #(.width(16)) s4 (.D(Write_Data), .en(and_5_out), .Q(s4_q), .clk(Register_CLOCK), .clr(Register_CLEAR));
  Register #(.width(16)) s5 (.D(Write_Data), .en(and_6_out), .Q(s5_q), .clk(Register_CLOCK), .clr(Register_CLEAR));
  Register #(.width(16)) s6 (.D(Write_Data), .en(and_7_out), .Q(s6_q), .clk(Register_CLOCK), .clr(Register_CLEAR));
  Register #(.width(16)) s7 (.D(Write_Data), .en(and_8_out), .Q(s7_q), .clk(Register_CLOCK), .clr(Register_CLEAR));
  Register #(.width(16)) s8 (.D(Write_Data), .en(and_9_out), .Q(s8_q), .clk(Register_CLOCK), .clr(Register_CLEAR));
  Register #(.width(16)) s9 (.D(Write_Data), .en(and_10_out), .Q(s9_q), .clk(Register_CLOCK), .clr(Register_CLEAR));
  Register #(.width(16)) s10 (.D(Write_Data), .en(and_11_out), .Q(s10_q), .clk(Register_CLOCK), .clr(Register_CLEAR));
  Register #(.width(16)) s11 (.D(Write_Data), .en(and_12_out), .Q(s11_q), .clk(Register_CLOCK), .clr(Register_CLEAR));
  Register #(.width(16)) s12 (.D(Write_Data), .en(and_13_out), .Q(s12_q), .clk(Register_CLOCK), .clr(Register_CLEAR));
  Register #(.width(16)) s13 (.D(Write_Data), .en(and_14_out), .Q(s13_q), .clk(Register_CLOCK), .clr(Register_CLEAR));
  Register #(.width(16)) s14 (.D(Write_Data), .en(and_15_out), .Q(s14_q), .clk(Register_CLOCK), .clr(Register_CLEAR));
  Register #(.width(16)) s15 (.D(Write_Data), .en(and_16_out), .Q(s15_q), .clk(Register_CLOCK), .clr(Register_CLEAR));
  Multiplexer #(.select(4), .width(16), .enable("false")) multiplexer_1 (
    .in0(s0_q), .in1(s1_q), .in2(s2_q), .in3(s3_q), .in4(s4_q), .in5(s5_q), .in6(s6_q), .in7(s7_q),
    .in8(s8_q), .in9(s9_q), .in10(s10_q), .in11(s11_q), .in12(s12_q), .in13(s13_q), .in14(s14_q),
    .in15(s15_q), .out(Data_1_Out), .sel(RS_Selector));
  Multiplexer #(.select(4), .width(16), .enable("false")) multiplexer_2 (
    .in0(s0_q), .in1(s1_q), .in2(s2_q), .in3(s3_q), .in4(s4_q), .in5(s5_q), .in6(s6_q), .in7(s7_q),
    .in8(s8_q), .in9(s9_q), .in10(s10_q), .in11(s11_q), .in12(s12_q), .in13(s13_q), .in14(s14_q),
    .in15(s15_q), .out(Data_2_Out), .sel(RT_Selector));

  // Notes on the sheet:
  //   Md Ulfat Tahsin_1913057642
endmodule

module Md_Ulfat_Tahsin_1913057642_Lab_Task5 (
  input  [15:0] Write_Data,
  input  W_en,
  input  CLR,
  output [3:0] Opcode,
  output [3:0] RS,
  output [3:0] RT,
  output [3:0] RD,
  output [15:0] Data_1,
  output [15:0] Data_2
);

  wire Clock_out;
  wire [15:0] adder_1_out, register_1_q;

  Register #(.width(16)) register_1 (.D(adder_1_out), .Q(register_1_q), .clk(Clock_out));  // open: en, clr
  Clock Clock (.out(Clock_out));
  // Probe on Write_Data
  Adder #(.width(16)) adder_1 (.a(register_1_q), .b(16'h1), .out(adder_1_out));  // open: cin, cout
  ROM #(.addrWidth(16), .dataWidth(16)) rom_1 (.addr(register_1_q), .data({Opcode, RS, RT, RD}));  // open: sel
  _16_bit_register_file u_16_bit_register_file_1 (
    .Write_Data(Write_Data), .Write_enabler(W_en), .RT_Selector(RT), .RD_Selector(RD),
    .Register_CLOCK(Clock_out), .Data_1_Out(Data_1), .RS_Selector(RS), .Data_2_Out(Data_2),
    .Register_CLEAR(CLR));
  // Probe on Data_1
  // Probe on Data_2

  // Notes on the sheet:
  //   Instruction counter
  //   contents of rom_1 (hex, n*v repeats v):
  //   5555 3 300 56f 1 108 100 102 8 8 8 110 f ff0
  //   Md Ulfat Tahsin_1913057
  //   Data 1 shows output from RS
  //   Data 2 shows output from RT
endmodule

module ex (
  input  [15:0] Write_Data,
  input  [1:0] operation,
  input  Cin,
  input  W_en,
  input  CLR,
  input  [1:0] operation_2,
  input  Cin_2,
  input  a_invert,
  input  b_invert,
  input  a_invert_2,
  input  b_invert_2,
  output [3:0] Opcode,
  output [3:0] RS,
  output [3:0] RT,
  output [3:0] RD,
  output [15:0] Data_1,
  output [15:0] ALU_out,
  output [15:0] Data_2
);

  wire Clock_out;
  wire [15:0] adder_1_p3, register_1_q;

  Register #(.width(16)) register_1 (.D(adder_1_p3), .Q(register_1_q), .clk(Clock_out));  // open: en, clr
  Clock Clock (.out(Clock_out));
  // Probe on Write_Data
  // Adder #(.width(16)) adder_1: pin names not known; wires that end beside it: register_1_q, 16'h1, adder_1_p3
  ROM #(.addrWidth(16), .dataWidth(16)) rom_1 (.addr(register_1_q), .data({Opcode, RS, RT, RD}));  // open: sel
  _16_bit_register_file u_16_bit_register_file_1 (
    .Write_Data(ALU_out), .Write_enabler(W_en), .RT_Selector(RT), .RD_Selector(RD),
    .Register_CLOCK(Clock_out), .Data_1_Out(Data_1), .RS_Selector(RS), .Data_2_Out(Data_2),
    .Register_CLEAR(CLR));
  // Probe on Data_1
  // Probe on Data_2
  // Probe on ALU_out

  // Notes on the sheet:
  //   Instruction counter
  //   contents of rom_1 (hex, n*v repeats v):
  //   0 0 0 56f 1 108 100 102 13*0 100 200 2 1 1 110
  //   Md Ulfat Tahsin_1913057
  //   Data 1 shows output from RS
  //   Data 2 shows output from RT
endmodule

module _1_bit_adder (
  input  A1,
  input  B1,
  input  Carry_in,
  output SUM1,
  output Cout
);

  wire and_1_out, and_2_out, xor_1_out;

  xor xor_1 (xor_1_out, A1, B1);
  and and_1 (and_1_out, xor_1_out, Carry_in);
  and and_2 (and_2_out, A1, B1);
  xor xor_2 (SUM1, xor_1_out, Carry_in);
  or or_1 (Cout, and_1_out, and_2_out);
endmodule

module _2_1_bit_ALU (
  input  a,
  input  Ain,
  input  Cin_for_adder,
  input  b,
  input  [1:0] ALU_Op,
  input  Bin,
  output out_7,
  output out_8
);

  wire and_1_out, multiplexer_1_out, multiplexer_2_out, n1_bit_adder_1_sum1, not_1_out, not_2_out, or_1_out,
       xor_1_out;

  not not_1 (not_1_out, a);
  not not_2 (not_2_out, b);
  Multiplexer #(.enable("false")) multiplexer_1 (.in0(a), .in1(not_1_out), .out(multiplexer_1_out), .sel(Ain));
  Multiplexer #(.enable("false")) multiplexer_2 (.in0(b), .in1(not_2_out), .out(multiplexer_2_out), .sel(Bin));
  and and_1 (and_1_out, multiplexer_1_out, multiplexer_2_out);
  or or_1 (or_1_out, multiplexer_1_out, multiplexer_2_out);
  _1_bit_adder u_1_bit_adder_1 (
    .A1(multiplexer_1_out), .B1(multiplexer_2_out), .Carry_in(Cin_for_adder), .SUM1(n1_bit_adder_1_sum1),
    .Cout(out_8));
  xor xor_1 (xor_1_out, multiplexer_1_out, multiplexer_2_out);
  Multiplexer #(.select(2), .enable("false")) multiplexer_3 (
    .in0(and_1_out), .in1(or_1_out), .in2(n1_bit_adder_1_sum1), .in3(xor_1_out), .out(out_7), .sel(ALU_Op));
  // Probe on out_7
endmodule

module _2_16_bi_ALU (
  input  Cin,
  input  [15:0] a,
  input  [15:0] b,
  input  [1:0] Operation,
  input  Ain,
  input  Bin,
  output [15:0] S,
  output Zero_Signal,
  output out_9
);

  wire n2_1_bit_alu_1_out_8, n2_1_bit_alu_2_out_8, n2_1_bit_alu_3_out_8, n2_1_bit_alu_4_out_8,
       n2_1_bit_alu_5_out_8, n2_1_bit_alu_6_out_8, n2_1_bit_alu_7_out_8, n2_1_bit_alu_8_out_8,
       n2_1_bit_alu_9_out_8, n2_1_bit_alu_10_out_8, n2_1_bit_alu_11_out_8, n2_1_bit_alu_12_out_8,
       n2_1_bit_alu_13_out_8, n2_1_bit_alu_14_out_8, n2_1_bit_alu_15_out_8, n2_1_bit_alu_16_out_8;

  // Probe on a
  // Probe on b
  _2_1_bit_ALU u_2_1_bit_alu_1 (
    .a(a[0]), .Ain(Ain), .Cin_for_adder(Cin), .b(b[0]), .Bin(Bin), .out_7(S[0]),
    .out_8(n2_1_bit_alu_1_out_8), .ALU_Op(Operation));
  _2_1_bit_ALU u_2_1_bit_alu_2 (
    .a(a[1]), .Ain(Ain), .Cin_for_adder(n2_1_bit_alu_1_out_8), .b(b[1]), .Bin(Bin), .out_7(S[1]),
    .out_8(n2_1_bit_alu_2_out_8), .ALU_Op(Operation));
  _2_1_bit_ALU u_2_1_bit_alu_3 (
    .a(a[2]), .Ain(Ain), .Cin_for_adder(n2_1_bit_alu_2_out_8), .b(b[2]), .Bin(Bin), .out_7(S[2]),
    .out_8(n2_1_bit_alu_3_out_8), .ALU_Op(Operation));
  _2_1_bit_ALU u_2_1_bit_alu_4 (
    .a(a[3]), .Ain(Ain), .Cin_for_adder(n2_1_bit_alu_3_out_8), .b(b[3]), .Bin(Bin), .out_7(S[3]),
    .out_8(n2_1_bit_alu_4_out_8), .ALU_Op(Operation));
  // Probe on S
  _2_1_bit_ALU u_2_1_bit_alu_5 (
    .a(a[4]), .Ain(Ain), .Cin_for_adder(n2_1_bit_alu_4_out_8), .b(b[4]), .Bin(Bin), .out_7(S[4]),
    .out_8(n2_1_bit_alu_5_out_8), .ALU_Op(Operation));
  _2_1_bit_ALU u_2_1_bit_alu_6 (
    .a(a[5]), .Ain(Ain), .Cin_for_adder(n2_1_bit_alu_5_out_8), .b(b[5]), .Bin(Bin), .out_7(S[5]),
    .out_8(n2_1_bit_alu_6_out_8), .ALU_Op(Operation));
  _2_1_bit_ALU u_2_1_bit_alu_7 (
    .a(a[6]), .Ain(Ain), .Cin_for_adder(n2_1_bit_alu_6_out_8), .b(b[6]), .Bin(Bin), .out_7(S[6]),
    .out_8(n2_1_bit_alu_7_out_8), .ALU_Op(Operation));
  _2_1_bit_ALU u_2_1_bit_alu_8 (
    .a(a[7]), .Ain(Ain), .Cin_for_adder(n2_1_bit_alu_7_out_8), .b(b[7]), .Bin(Bin), .out_7(S[7]),
    .out_8(n2_1_bit_alu_8_out_8), .ALU_Op(Operation));
  _2_1_bit_ALU u_2_1_bit_alu_9 (
    .a(a[8]), .Ain(Ain), .Cin_for_adder(n2_1_bit_alu_8_out_8), .b(b[8]), .Bin(Bin), .out_7(S[8]),
    .out_8(n2_1_bit_alu_9_out_8), .ALU_Op(Operation));
  _2_1_bit_ALU u_2_1_bit_alu_10 (
    .a(a[9]), .Ain(Ain), .Cin_for_adder(n2_1_bit_alu_9_out_8), .b(b[9]), .Bin(Bin), .out_7(S[9]),
    .out_8(n2_1_bit_alu_10_out_8), .ALU_Op(Operation));
  _2_1_bit_ALU u_2_1_bit_alu_11 (
    .a(a[10]), .Ain(Ain), .Cin_for_adder(n2_1_bit_alu_10_out_8), .b(b[10]), .Bin(Bin), .out_7(S[10]),
    .out_8(n2_1_bit_alu_11_out_8), .ALU_Op(Operation));
  _2_1_bit_ALU u_2_1_bit_alu_12 (
    .a(a[11]), .Ain(Ain), .Cin_for_adder(n2_1_bit_alu_11_out_8), .b(b[11]), .Bin(Bin), .out_7(S[11]),
    .out_8(n2_1_bit_alu_12_out_8), .ALU_Op(Operation));
  _2_1_bit_ALU u_2_1_bit_alu_13 (
    .a(a[12]), .Ain(Ain), .Cin_for_adder(n2_1_bit_alu_12_out_8), .b(b[12]), .Bin(Bin), .out_7(S[12]),
    .out_8(n2_1_bit_alu_13_out_8), .ALU_Op(Operation));
  _2_1_bit_ALU u_2_1_bit_alu_14 (
    .a(a[13]), .Ain(Ain), .Cin_for_adder(n2_1_bit_alu_13_out_8), .b(b[13]), .Bin(Bin), .out_7(S[13]),
    .out_8(n2_1_bit_alu_14_out_8), .ALU_Op(Operation));
  _2_1_bit_ALU u_2_1_bit_alu_15 (
    .a(a[14]), .Ain(Ain), .Cin_for_adder(n2_1_bit_alu_14_out_8), .b(b[14]), .Bin(Bin), .out_7(S[14]),
    .out_8(n2_1_bit_alu_15_out_8), .ALU_Op(Operation));
  _2_1_bit_ALU u_2_1_bit_alu_16 (
    .a(a[15]), .Ain(Ain), .Cin_for_adder(n2_1_bit_alu_15_out_8), .b(b[15]), .Bin(Bin), .out_7(S[15]),
    .out_8(n2_1_bit_alu_16_out_8), .ALU_Op(Operation));
  xor xor_1 (out_9, n2_1_bit_alu_15_out_8, n2_1_bit_alu_16_out_8);
  nor u_Zero_SIgnal (Zero_Signal, S[0], S[1], S[2], S[3], S[4], S[5], S[6], S[7], S[8], S[9], S[10], S[11], S[12], S[13], S[14], S[15]);

  // Notes on the sheet:
  //   Zero Signal
endmodule

module R_type (
  input  [1:0] ALU_Opcode,
  input  Cin,
  input  [15:0] Write_Data,
  input  Ain,
  input  Bin,
  input  W_en,
  input  CLR,
  output [3:0] Opcode,
  output [3:0] RS,
  output [3:0] RT,
  output [3:0] RD,
  output [15:0] Data_1,
  output Beq_Zero_Signal,
  output [15:0] S,
  output Overflow1,
  output [15:0] Data_2
);

  wire Clock_out;
  wire [15:0] adder_1_out, register_1_q;

  Register #(.width(16)) register_1 (.D(adder_1_out), .Q(register_1_q), .clk(Clock_out));  // open: en, clr
  Clock Clock (.out(Clock_out));
  // Probe on Write_Data
  Adder #(.width(16)) adder_1 (.a(register_1_q), .b(16'h1), .out(adder_1_out));  // open: cin, cout
  ROM #(.addrWidth(16), .dataWidth(16)) rom_1 (.addr(register_1_q), .data({Opcode, RS, RT, RD}));  // open: sel
  _16_bit_register_file u_16_bit_register_file_1 (
    .Write_Data(S), .Write_enabler(W_en), .RT_Selector(RT), .RD_Selector(RD), .Register_CLOCK(Clock_out),
    .Data_1_Out(Data_1), .RS_Selector(RS), .Data_2_Out(Data_2), .Register_CLEAR(CLR));
  // Probe on Data_1
  // Probe on Data_2
  _2_16_bi_ALU u_2_16_bi_alu_1 (
    .a(Data_1), .b(Data_2), .Operation(ALU_Opcode), .Ain(Ain), .Bin(Bin), .S(S), .out_9(Overflow1),
    .Cin(Cin), .Zero_Signal(Beq_Zero_Signal));
  // Probe on S

  // Notes on the sheet:
  //   Instruction counter
  //   contents of rom_1 (hex, n*v repeats v):
  //   12 200 300 56f 1 108 100 102 8 8 8 110 f ff0
  //   Md Ulfat Tahsin_1913057
  //   Data 1 shows output from RS
  //   Data 2 shows output from RT
endmodule

module I_type (
  input  [1:0] ALU_opcode,
  input  Cin,
  input  [15:0] Write_Data,
  input  Ain,
  input  Bin,
  input  RT_RD,
  input  W_en,
  input  CLR,
  output [3:0] Opcode,
  output [3:0] RS,
  output [3:0] RT,
  output [3:0] RD,
  output [15:0] Data_1,
  output Beq_Zero_Signal,
  output [15:0] S,
  output Overflow1,
  output [15:0] Data_2
);

  wire Clock_out;
  wire [3:0] multiplexer_1_out;
  wire [15:0] adder_1_out, register_1_q;

  Register #(.width(16)) register_1 (.D(adder_1_out), .Q(register_1_q), .clk(Clock_out));  // open: en, clr
  Clock Clock (.out(Clock_out));
  // Probe on Write_Data
  Adder #(.width(16)) adder_1 (.a(register_1_q), .b(16'h1), .out(adder_1_out));  // open: cin, cout
  ROM #(.addrWidth(16), .dataWidth(16)) rom_1 (.addr(register_1_q), .data({Opcode, RS, RT, RD}));  // open: sel
  Multiplexer #(.width(4), .enable("false")) multiplexer_1 (.in0(RT), .in1(RD), .out(multiplexer_1_out), .sel(RT_RD));
  assign Data_2 = {{12{1'b0}}, RD};  // Bit_Extender bit_extender_1
  _16_bit_register_file u_16_bit_register_file_1 (
    .Write_Data(S), .Write_enabler(W_en), .RT_Selector(multiplexer_1_out), .RD_Selector(multiplexer_1_out),
    .Register_CLOCK(Clock_out), .Data_1_Out(Data_1), .RS_Selector(RS), .Register_CLEAR(CLR));  // open: Data_2_Out
  // Probe on Data_1
  // Probe on Data_2
  _2_16_bi_ALU u_2_16_bi_alu_1 (
    .a(Data_1), .b(Data_2), .Operation(ALU_opcode), .Ain(Ain), .Bin(Bin), .S(S), .out_9(Overflow1),
    .Cin(Cin), .Zero_Signal(Beq_Zero_Signal));
  // Probe on S

  // Notes on the sheet:
  //   Instruction counter
  //   contents of rom_1 (hex, n*v repeats v):
  //   123 20 300 56f 1 108 100 102 8 8 8 110 f ff0
  //   Immediate for I-type
  //   Md Ulfat Tahsin_1913057
  //   Used for immediate type input to ALU
  //   Data 1 shows output from RS
  //   Data 2 shows output from RT
  //   Addi r1, r2, 3
endmodule

module Load_Store_type (
  input  [1:0] ALU_Opcode,
  input  Cin,
  input  [15:0] Write_Data,
  input  RT_RD,
  input  Ain,
  input  Bin,
  input  W_en,
  input  CLR,
  input  Store,
  input  Load,
  output [3:0] Opcode,
  output [3:0] RS,
  output [3:0] RT,
  output [3:0] RD,
  output [15:0] Data_1,
  output Beq_Zero_Signal,
  output [15:0] S,
  output Overflow1,
  output [15:0] Data_2,
  output [15:0] Loaded_value
);

  wire Clock_out, or_1_out;
  wire [3:0] multiplexer_1_out;
  wire [15:0] adder_1_out, bit_extender_1_out, register_1_q;

  Register #(.width(16)) register_1 (.D(adder_1_out), .Q(register_1_q), .clk(Clock_out));  // open: en, clr
  Clock Clock (.out(Clock_out));
  // Probe on Write_Data
  Adder #(.width(16)) adder_1 (.a(register_1_q), .b(16'h1), .out(adder_1_out));  // open: cin, cout
  ROM #(.addrWidth(16), .dataWidth(16)) rom_1 (.addr(register_1_q), .data({Opcode, RS, RT, RD}));  // open: sel
  Multiplexer #(.width(4), .enable("false")) multiplexer_1 (.in0(RT), .in1(RD), .out(multiplexer_1_out), .sel(RT_RD));
  assign bit_extender_1_out = {{12{1'b0}}, RD};  // Bit_Extender bit_extender_1
  _16_bit_register_file u_16_bit_register_file_1 (
    .Write_Data(S), .Write_enabler(W_en), .RT_Selector(multiplexer_1_out), .RD_Selector(multiplexer_1_out),
    .Register_CLOCK(Clock_out), .Data_1_Out(Data_1), .RS_Selector(RS), .Data_2_Out(Data_2),
    .Register_CLEAR(CLR));
  // Probe on Data_1
  // Probe on Data_2
  _2_16_bi_ALU u_2_16_bi_alu_1 (
    .a(Data_1), .b(bit_extender_1_out), .Operation(ALU_Opcode), .Ain(Ain), .Bin(Bin), .S(S),
    .out_9(Overflow1), .Cin(Cin), .Zero_Signal(Beq_Zero_Signal));
  RAM #(.addrWidth(16), .dataWidth(16), .bus("separate")) ram_1 (
    .addr(S), .din(Data_2), .data(Loaded_value), .str(Store), .sel(or_1_out), .clk(Clock_out), .ld(Load));  // open: clr
  or or_1 (or_1_out, Load, Store);
  // Probe on S
  // Probe on Loaded_value

  // Notes on the sheet:
  //   Instruction counter
  //   contents of rom_1 (hex, n*v repeats v):
  //   1 200 300 56f 1 108 100 102 8 8 8 110 f ff0
  //   Used here to determine offset as immediate value
  //   Md Ulfat Tahsin_1913057
  //   A is used to access the location
  //   D is used to write any data when storing
  //   Data 1 shows output from RS
  //   Or gate used to enable the RAM only when the load/store is being executed
  //   Data 2 shows output from RT
endmodule

module Datapath_all_formats (
  input  [1:0] ALU_Opcode,
  input  Cin,
  input  [15:0] Write_Data,
  input  Jump,
  input  RD_RT,
  input  in_6,
  input  Ain,
  input  Bin,
  input  W_en,
  input  CLR,
  input  Store,
  input  Load,
  input  ALU_load_store_MUX,
  output [3:0] Opcode,
  output [3:0] RS,
  output [3:0] RT,
  output [3:0] RD,
  output [15:0] Data_1,
  output Beq_Zero_Signal,
  output [15:0] S,
  output Overflow1,
  output [15:0] Data_2,
  output [15:0] Loaded_value
);

  wire Clock_out, or_1_out;
  wire [3:0] multiplexer_2_out;
  wire [15:0] adder_1_out, adder_2_out, bit_extender_1_out, bit_extender_2_out, multiplexer_1_out,
       multiplexer_3_out, multiplexer_4_out, PC_q;

  Multiplexer #(.width(16), .enable("false")) multiplexer_1 (
    .in0(adder_1_out), .in1(adder_2_out), .out(multiplexer_1_out), .sel(Jump));
  Register #(.width(16)) PC (.D(multiplexer_1_out), .Q(PC_q), .clk(Clock_out));  // open: en, clr
  Clock Clock (.out(Clock_out));
  // Probe on Write_Data
  Adder #(.width(16)) adder_1 (.a(PC_q), .b(16'h1), .out(adder_1_out));  // open: cin, cout
  ROM #(.addrWidth(16), .dataWidth(16)) rom_1 (.addr(PC_q), .data({Opcode, RS, RT, RD}));  // open: sel
  Multiplexer #(.width(4), .enable("false")) multiplexer_2 (.in0(RD), .in1(RT), .out(multiplexer_2_out), .sel(RD_RT));
  assign bit_extender_1_out = {{12{1'b0}}, RD};  // Bit_Extender bit_extender_1
  assign bit_extender_2_out = {{4{1'b0}}, {RS, RT, RD}};  // Bit_Extender bit_extender_2
  _16_bit_register_file u_16_bit_register_file_1 (
    .Write_Data(multiplexer_4_out), .Write_enabler(W_en), .RT_Selector(RT), .RD_Selector(multiplexer_2_out),
    .Register_CLOCK(Clock_out), .Data_1_Out(Data_1), .RS_Selector(RS), .Data_2_Out(Data_2),
    .Register_CLEAR(CLR));
  Adder #(.width(16)) adder_2 (.a(adder_1_out), .b(bit_extender_2_out), .out(adder_2_out));  // open: cin, cout
  // Probe on Data_1
  // Probe on Data_2
  Multiplexer #(.width(16), .enable("false")) multiplexer_3 (
    .in0(Data_2), .in1(bit_extender_1_out), .out(multiplexer_3_out), .sel(in_6));
  _2_16_bi_ALU u_2_16_bi_alu_1 (
    .a(Data_1), .b(multiplexer_3_out), .Operation(ALU_Opcode), .Ain(Ain), .Bin(Bin), .S(S),
    .out_9(Overflow1), .Cin(Cin), .Zero_Signal(Beq_Zero_Signal));
  RAM #(.addrWidth(16), .dataWidth(16), .bus("separate")) ram_1 (
    .addr(S), .din(Data_2), .data(Loaded_value), .str(Store), .sel(or_1_out), .clk(Clock_out), .ld(Load));  // open: clr
  or or_1 (or_1_out, Load, Store);
  // Probe on Loaded_value
  // Probe on S
  Multiplexer #(.width(16), .enable("false")) multiplexer_4 (
    .in0(S), .in1(Loaded_value), .out(multiplexer_4_out), .sel(ALU_load_store_MUX));

  // Notes on the sheet:
  //   4
  //   MUX4 is ised to get the target location for jump instructions
  //   Instruction counter
  //   contents of rom_1 (hex, n*v repeats v):
  //   1 200 300 56f 1 108 100 102 8 8 8 110 f ff0
  //   Used here to determine offset as immediate value
  //   1
  //   Md Ulfat Tahsin_1913057
  //   MUX1 used here to switch between R/I type
  //   A is used to access the location
  //   D is used to write any data when storing
  //   Data 1 shows output from RS
  //   Or gate used to enable the RAM only when the load/store is being executed
  //   2
  //   Data 2 shows output from RT
  //   3
  //   MUX3 here is used to either to choose the value directly from ALU or the effective address from RAM for lw/sw
endmodule
