// Logisim project Design of a 4 bit multiplier.circ as structural Verilog
module _7404___NOT_IC (
  input  in_1,
  input  in_2,
  input  in_3,
  input  in_4,
  input  in_5,
  input  in_6,
  output out_7,
  output out_8,
  output out_9,
  output out_10,
  output out_11,
  output out_12
);

  not not_1 (out_7, in_1);
  not not_2 (out_8, in_2);
  not not_3 (out_9, in_3);
  not not_4 (out_10, in_4);
  not not_5 (out_11, in_5);
  not not_6 (out_12, in_6);
endmodule

module _7408___AND_IC (
  input  in_1,
  input  in_2,
  input  in_3,
  input  in_4,
  input  in_5,
  input  in_6,
  input  in_7,
  input  in_8,
  output out_9,
  output out_10,
  output out_11,
  output out_12
);

  and and_1 (out_9, in_1, in_2);
  and and_2 (out_10, in_3, in_4);
  and and_3 (out_11, in_5, in_6);
  and and_4 (out_12, in_7, in_8);
endmodule

module _7432___OR_IC (
  input  in_1,
  input  in_2,
  input  in_3,
  input  in_4,
  input  in_5,
  input  in_6,
  input  in_7,
  input  in_8,
  output out_9,
  output out_10,
  output out_11,
  output out_12
);

  or or_1 (out_9, in_1, in_2);
  or or_2 (out_10, in_3, in_4);
  or or_3 (out_11, in_5, in_6);
  or or_4 (out_12, in_7, in_8);
endmodule

module _7486____XOR_IC (
  input  in_1,
  input  in_2,
  input  in_3,
  input  in_4,
  input  in_5,
  input  in_6,
  input  in_7,
  input  in_8,
  output out_9,
  output out_10,
  output out_11,
  output out_12
);

  xor xor_1 (out_9, in_1, in_2);
  xor xor_2 (out_10, in_3, in_4);
  xor xor_3 (out_11, in_5, in_6);
  xor xor_4 (out_12, in_7, in_8);
endmodule

module _4_1_MUX_Circuit (
  input  I1,
  input  I2,
  input  I3,
  input  I4,
  input  S2,
  input  S1,
  output out_7
);

  wire and_1_out, and_2_out, and_3_out, and_4_out, not_1_out, not_2_out;

  not not_1 (not_1_out, S2);
  not not_2 (not_2_out, S1);
  and and_1 (and_1_out, not_1_out, I1, not_2_out);
  and and_2 (and_2_out, not_1_out, I2, S1);
  and and_3 (and_3_out, S2, I3, not_2_out);
  and and_4 (and_4_out, S2, I4, S1);
  or or_1 (out_7, and_1_out, and_2_out, and_3_out, and_4_out);
endmodule

module Lab_Task_1 (
  input  A1,
  input  B1,
  input  A2,
  input  B2,
  input  S2,
  input  S1,
  output F1,
  output F2
);

  wire n7404_not_ic_1_out_7, n7404_not_ic_1_out_8, n7408_and_ic_1_out_9, n7408_and_ic_1_out_10,
       n7432_or_ic_1_out_9, n7432_or_ic_1_out_10, n7486_xor_ic_1_out_9, n7486_xor_ic_1_out_10;

  _7408___AND_IC u_7408_and_ic_1 (
    .in_1(A1), .in_2(B1), .in_3(A2), .in_4(B2), .out_9(n7408_and_ic_1_out_9), .out_10(n7408_and_ic_1_out_10));  // open: in_5, in_6, in_7, in_8, out_11, out_12
  _7432___OR_IC u_7432_or_ic_1 (
    .in_1(A1), .in_2(B1), .in_3(A2), .in_4(B2), .out_9(n7432_or_ic_1_out_9), .out_10(n7432_or_ic_1_out_10));  // open: in_5, in_6, in_7, in_8, out_11, out_12
  _7404___NOT_IC u_7404_not_ic_1 (
    .in_1(A1), .in_2(A2), .out_7(n7404_not_ic_1_out_7), .out_8(n7404_not_ic_1_out_8));  // open: in_3, in_4, in_5, in_6, out_9, out_10, out_11, out_12
  _7486____XOR_IC u_7486_xor_ic_1 (
    .in_1(A1), .in_2(B1), .in_3(A2), .in_4(B2), .out_9(n7486_xor_ic_1_out_9), .out_10(n7486_xor_ic_1_out_10));  // open: in_5, in_6, in_7, in_8, out_11, out_12
  _4_1_MUX_Circuit u_4_1_mux_circuit_1 (
    .I1(n7408_and_ic_1_out_9), .I2(n7432_or_ic_1_out_9), .I3(n7404_not_ic_1_out_7),
    .I4(n7486_xor_ic_1_out_9), .S2(S2), .S1(S1), .out_7(F1));
  _4_1_MUX_Circuit u_4_1_mux_circuit_2 (
    .I1(n7408_and_ic_1_out_10), .I2(n7432_or_ic_1_out_10), .I3(n7404_not_ic_1_out_8),
    .I4(n7486_xor_ic_1_out_10), .S2(S2), .S1(S1), .out_7(F2));

  // Notes on the sheet:
  //   MD ULFAT TAHSIN_1913057642
endmodule

module D_Flip_Flop (
  input  SET,
  input  Clock,
  input  Data,
  input  RESET,
  output Q,
  output Q_prime
);

  wire nand_1_out, nand_2_out, nand_3_out, nand_4_out, not_1_out, not_2_out;

  not not_1 (not_1_out, SET);
  not not_2 (not_2_out, RESET);
  nand nand_1 (nand_1_out, not_1_out, nand_4_out, nand_2_out);
  nand nand_2 (nand_2_out, nand_1_out, Clock, not_2_out);
  nand nand_3 (nand_3_out, nand_2_out, Clock, nand_4_out);
  nand nand_4 (nand_4_out, nand_3_out, Data, not_2_out);
  nand nand_5 (Q, not_1_out, nand_2_out, Q_prime);
  nand nand_6 (Q_prime, Q, nand_3_out, not_2_out);

  // Notes on the sheet:
  //   Md Ulfat Tahsin_1913057642_D-Flip Flop
endmodule

module _4_Bit_Adder (
  input  A1,
  input  B1,
  input  Carry_in,
  input  A2,
  input  B2,
  input  A3,
  input  B3,
  input  A4,
  input  B4,
  output SUM1,
  output SUM2,
  output SUM3,
  output SUM4,
  output CARRY_Cout
);

  wire and_1_out, and_2_out, and_3_out, and_4_out, and_5_out, and_6_out, and_7_out, and_8_out, or_1_out,
       or_2_out, or_3_out, xor_1_out, xor_2_out, xor_3_out, xor_4_out;

  and and_1 (and_1_out, A3, B3);
  and and_2 (and_2_out, A4, B4);
  xor xor_1 (xor_1_out, A1, B1);
  and and_3 (and_3_out, xor_1_out, Carry_in);
  and and_4 (and_4_out, A1, B1);
  xor xor_2 (xor_2_out, A2, B2);
  and and_5 (and_5_out, xor_2_out, or_1_out);
  and and_6 (and_6_out, A2, B2);
  xor xor_3 (xor_3_out, A3, B3);
  and and_7 (and_7_out, xor_3_out, or_2_out);
  xor xor_4 (xor_4_out, A4, B4);
  and and_8 (and_8_out, xor_4_out, or_3_out);
  xor xor_5 (SUM1, xor_1_out, Carry_in);
  or or_1 (or_1_out, and_3_out, and_4_out);
  xor xor_6 (SUM2, xor_2_out, or_1_out);
  or or_2 (or_2_out, and_5_out, and_6_out);
  xor xor_7 (SUM3, xor_3_out, or_2_out);
  or or_3 (or_3_out, and_7_out, and_1_out);
  xor xor_8 (SUM4, xor_4_out, or_3_out);
  or or_4 (CARRY_Cout, and_8_out, and_2_out);

  // Notes on the sheet:
  //   Md Ulfat Tahsin_1913057642_4-Bit Adder
endmodule

module Lab_Task_2 (
  input  B4,
  input  B3,
  input  B2,
  input  B1,
  input  A4,
  input  A3,
  input  A2,
  input  A1,
  input  Cin,
  input  _0,
  input  S2,
  input  S1,
  output Cout,
  output S4,
  output S3,
  output S2_2,
  output out_17
);

  wire n4_1_mux_circuit_1_out_7, n4_1_mux_circuit_2_out_7, n4_1_mux_circuit_3_out_7,
       n4_1_mux_circuit_4_out_7, n7404_not_ic_1_out_7, n7404_not_ic_1_out_8, n7404_not_ic_1_out_10,
       n7404_not_ic_1_out_11, not_1_out;

  _7404___NOT_IC u_7404_not_ic_1 (
    .in_1(B4), .in_2(B3), .in_4(B2), .in_5(B1), .out_7(n7404_not_ic_1_out_7), .out_8(n7404_not_ic_1_out_8),
    .out_10(n7404_not_ic_1_out_10), .out_11(n7404_not_ic_1_out_11));  // open: in_3, in_6, out_9, out_12
  not not_1 (not_1_out, _0);
  _4_1_MUX_Circuit u_4_1_mux_circuit_1 (
    .I1(B1), .I2(n7404_not_ic_1_out_11), .I3(_0), .I4(not_1_out), .S2(S2), .S1(S1),
    .out_7(n4_1_mux_circuit_1_out_7));
  _4_1_MUX_Circuit u_4_1_mux_circuit_2 (
    .I1(B2), .I2(n7404_not_ic_1_out_10), .I3(_0), .I4(not_1_out), .S2(S2), .S1(S1),
    .out_7(n4_1_mux_circuit_2_out_7));
  _4_1_MUX_Circuit u_4_1_mux_circuit_3 (
    .I1(B3), .I2(n7404_not_ic_1_out_8), .I3(_0), .I4(not_1_out), .S2(S2), .S1(S1),
    .out_7(n4_1_mux_circuit_3_out_7));
  _4_1_MUX_Circuit u_4_1_mux_circuit_4 (
    .I1(B4), .I2(n7404_not_ic_1_out_7), .I3(_0), .I4(not_1_out), .S2(S2), .S1(S1),
    .out_7(n4_1_mux_circuit_4_out_7));
  _4_Bit_Adder u_4_bit_adder_1 (
    .A1(A1), .B1(n4_1_mux_circuit_1_out_7), .Carry_in(Cin), .A2(A2), .B2(n4_1_mux_circuit_2_out_7), .A3(A3),
    .B3(n4_1_mux_circuit_3_out_7), .A4(A4), .B4(n4_1_mux_circuit_4_out_7), .SUM1(out_17), .SUM2(S2_2),
    .SUM3(S3), .SUM4(S4), .CARRY_Cout(Cout));

  // Notes on the sheet:
  //   1
  //   Md Ulfat Tahsin_1913057642
endmodule

module Lab_Task_3 (
  input  _0,
  input  B4,
  input  B3,
  input  B2,
  input  B1,
  input  A4,
  input  A3,
  input  A2,
  input  A1,
  input  Cin,
  output S8,
  output S7,
  output S6,
  output S5,
  output S4,
  output S3,
  output S2,
  output S1
);

  wire n4_bit_adder_1_carry_cout, n4_bit_adder_1_sum2, n4_bit_adder_1_sum3, n4_bit_adder_1_sum4,
       n4_bit_adder_2_carry_cout, n4_bit_adder_2_sum2, n4_bit_adder_2_sum3, n4_bit_adder_2_sum4,
       n7408_and_ic_1_out_10, n7408_and_ic_1_out_11, n7408_and_ic_1_out_12, n7408_and_ic_2_out_9,
       n7408_and_ic_2_out_10, n7408_and_ic_2_out_11, n7408_and_ic_2_out_12, n7408_and_ic_3_out_9,
       n7408_and_ic_3_out_10, n7408_and_ic_3_out_11, n7408_and_ic_3_out_12, n7408_and_ic_4_out_9,
       n7408_and_ic_4_out_10, n7408_and_ic_4_out_11, n7408_and_ic_4_out_12;

  _7408___AND_IC u_7408_and_ic_1 (
    .in_1(A1), .in_2(B1), .in_3(A1), .in_4(B2), .in_5(A1), .in_6(B4), .in_7(A1), .in_8(B3), .out_9(S1),
    .out_10(n7408_and_ic_1_out_10), .out_11(n7408_and_ic_1_out_11), .out_12(n7408_and_ic_1_out_12));
  _7408___AND_IC u_7408_and_ic_2 (
    .in_1(A2), .in_2(B1), .in_3(A2), .in_4(B2), .in_5(B4), .in_6(A2), .in_7(A2), .in_8(B3),
    .out_9(n7408_and_ic_2_out_9), .out_10(n7408_and_ic_2_out_10), .out_11(n7408_and_ic_2_out_11),
    .out_12(n7408_and_ic_2_out_12));
  _7408___AND_IC u_7408_and_ic_3 (
    .in_1(A3), .in_2(B1), .in_3(A3), .in_4(B2), .in_5(A3), .in_6(B4), .in_7(A3), .in_8(B3),
    .out_9(n7408_and_ic_3_out_9), .out_10(n7408_and_ic_3_out_10), .out_11(n7408_and_ic_3_out_11),
    .out_12(n7408_and_ic_3_out_12));
  _7408___AND_IC u_7408_and_ic_4 (
    .in_1(A4), .in_2(B1), .in_3(A4), .in_4(B2), .in_5(B4), .in_6(A4), .in_7(A4), .in_8(B3),
    .out_9(n7408_and_ic_4_out_9), .out_10(n7408_and_ic_4_out_10), .out_11(n7408_and_ic_4_out_11),
    .out_12(n7408_and_ic_4_out_12));
  _4_Bit_Adder u_4_bit_adder_1 (
    .A1(n7408_and_ic_1_out_10), .B1(n7408_and_ic_2_out_9), .Carry_in(Cin), .A2(n7408_and_ic_1_out_12),
    .B2(n7408_and_ic_2_out_10), .A3(n7408_and_ic_1_out_11), .B3(n7408_and_ic_2_out_12), .A4(_0),
    .B4(n7408_and_ic_2_out_11), .SUM1(S2), .SUM2(n4_bit_adder_1_sum2), .SUM3(n4_bit_adder_1_sum3),
    .SUM4(n4_bit_adder_1_sum4), .CARRY_Cout(n4_bit_adder_1_carry_cout));
  _4_Bit_Adder u_4_bit_adder_2 (
    .A1(n4_bit_adder_1_sum2), .B1(n7408_and_ic_3_out_9), .Carry_in(Cin), .A2(n4_bit_adder_1_sum3),
    .B2(n7408_and_ic_3_out_10), .A3(n4_bit_adder_1_sum4), .B3(n7408_and_ic_3_out_12),
    .A4(n4_bit_adder_1_carry_cout), .B4(n7408_and_ic_3_out_11), .SUM1(S3), .SUM2(n4_bit_adder_2_sum2),
    .SUM3(n4_bit_adder_2_sum3), .SUM4(n4_bit_adder_2_sum4), .CARRY_Cout(n4_bit_adder_2_carry_cout));
  _4_Bit_Adder u_4_bit_adder_3 (
    .A1(n4_bit_adder_2_sum2), .B1(n7408_and_ic_4_out_9), .Carry_in(Cin), .A2(n4_bit_adder_2_sum3),
    .B2(n7408_and_ic_4_out_10), .A3(n4_bit_adder_2_sum4), .B3(n7408_and_ic_4_out_12),
    .A4(n4_bit_adder_2_carry_cout), .B4(n7408_and_ic_4_out_11), .SUM1(S4), .SUM2(S5), .SUM3(S6), .SUM4(S7),
    .CARRY_Cout(S8));

  // Notes on the sheet:
  //   MD ULFAT TAHSIN_1913057642
endmodule
