// Logisim project MIPS Architecture (Datapath and Control Unit).circ as structural Verilog: 18 circuits, main circuit Datapath all formats
module main (
  input  [13:0] in_1,
  input  [3:0] in_2
);

  wire bit_extender_1_out, n16_bit_register_file_1_p1, n16_bit_register_file_1_p2,
       n16_bit_register_file_1_p3, n16_bit_register_file_1_p5, undriven;

  Multiplexer #(.width(16), .enable("false")) multiplexer_1 ();  // open: in0, in1, out, sel
  Bit_Extender #(.in_width(2), .out_width(1)) bit_extender_1 (.in(in_1[1:0]), .out(bit_extender_1_out));
  // _16_bit_register_file 16_bit_register_file_1: pin names not known; wires that end beside it: n16_bit_register_file_1_p1, n16_bit_register_file_1_p2, n16_bit_register_file_1_p3, in_2, n16_bit_register_file_1_p5
  _7_Segment_Display u_7_segment_display_1 (
    .g(undriven), .f(bit_extender_1_out), .a(bit_extender_1_out), .e(bit_extender_1_out),
    .d(n16_bit_register_file_1_p5), .c(bit_extender_1_out), .dp(bit_extender_1_out));  // open: b

  // Notes on the sheet:
  //   op_code_for_in    hexa_value_for_data
endmodule

module _16_bit_register_file (
  input  [15:0] Write_Data,
  input  Write_enabler,
  input  [3:0] RS_Selector,
  input  [3:0] RT_Selector,
  input  [3:0] RD_Selector,
  input  Register_CLOCK,
  input  Register_CLEAR,
  output [15:0] Data_1_Out,
  output [15:0] Data_2_Out
);

  wire and_1_out, and_2_out, and_3_out, and_4_out, and_5_out, and_6_out, and_7_out, and_8_out, and_9_out,
       and_10_out, and_11_out, and_12_out, and_13_out, and_14_out, and_15_out, and_16_out, decoder_1_out0,
       decoder_1_out1, decoder_1_out2, decoder_1_out3, decoder_1_out4, decoder_1_out5, decoder_1_out6,
       decoder_1_out7, decoder_1_out8, decoder_1_out9, decoder_1_out10, decoder_1_out11, decoder_1_out12,
       decoder_1_out13, decoder_1_out14, decoder_1_out15;
  wire [15:0] s0_q, s1_q, s2_q, s3_q, s4_q, s5_q, s6_q, s7_q, s8_q, s9_q, s10_q, s11_q, s12_q, s13_q, s14_q,
       s15_q;

  Decoder #(.select(4), .enable("false")) decoder_1 (
    .out0(decoder_1_out0), .out1(decoder_1_out1), .out2(decoder_1_out2), .out3(decoder_1_out3),
    .out4(decoder_1_out4), .out5(decoder_1_out5), .out6(decoder_1_out6), .out7(decoder_1_out7),
    .out8(decoder_1_out8), .out9(decoder_1_out9), .out10(decoder_1_out10), .out11(decoder_1_out11),
    .out12(decoder_1_out12), .out13(decoder_1_out13), .out14(decoder_1_out14), .out15(decoder_1_out15),
    .sel(RD_Selector));
  and and_1 (and_1_out, decoder_1_out0, Write_enabler);
  and and_2 (and_2_out, decoder_1_out1, Write_enabler);
  and and_3 (and_3_out, decoder_1_out2, Write_enabler);
  and and_4 (and_4_out, decoder_1_out3, Write_enabler);
  and and_5 (and_5_out, decoder_1_out4, Write_enabler);
  and and_6 (and_6_out, decoder_1_out5, Write_enabler);
  and and_7 (and_7_out, decoder_1_out6, Write_enabler);
  and and_8 (and_8_out, decoder_1_out7, Write_enabler);
  and and_9 (and_9_out, decoder_1_out8, Write_enabler);
  and and_10 (and_10_out, decoder_1_out9, Write_enabler);
  and and_11 (and_11_out, decoder_1_out10, Write_enabler);
  and and_12 (and_12_out, decoder_1_out11, Write_enabler);
  and and_13 (and_13_out, decoder_1_out12, Write_enabler);
  and and_14 (and_14_out, decoder_1_out13, Write_enabler);
  and and_15 (and_15_out, decoder_1_out14, Write_enabler);
  and and_16 (and_16_out, decoder_1_out15, Write_enabler);
  Register #(.width(16)) s0 (.D(Write_Data), .en(and_1_out), .Q(s0_q), .clk(Register_CLOCK), .clr(Register_CLEAR));
  Register #(.width(16)) s1 (.D(Write_Data), .en(and_2_out), .Q(s1_q), .clk(Register_CLOCK), .clr(Register_CLEAR));
  Register #(.width(16)) s2 (.D(Write_Data), .en(and_3_out), .Q(s2_q), .clk(Register_CLOCK), .clr(Register_CLEAR));
  Register #(.width(16)) s3 (.D(Write_Data), .en(and_4_out), .Q(s3_q), .clk(Register_CLOCK), .clr(Register_CLEAR));
  Register #(.width(16)) s4 (.D(Write_Data), .en(and_5_out), .Q(s4_q), .clk(Register_CLOCK), .clr(Register_CLEAR));
  Register #(.width(16)) s5 (.D(Write_Data), .en(and_6_out), .Q(s5_q), .clk(Register_CLOCK), .clr(Register_CLEAR));
  Register #(.width(16)) s6 (.D(Write_Data), .en(and_7_out), .Q(s6_q), .clk(Register_CLOCK), .clr(Register_CLEAR));
  Register #(.width(16)) s7 (.D(Write_Data), .en(and_8_out), .Q(s7_q), .clk(Register_CLOCK), .clr(Register_CLEAR));
  Register #(.width(16)) s8 (.D(Write_Data), .en(and_9_out), .Q(s8_q), .clk(Register_CLOCK), .clr(Register_CLEAR));
  Register #(.width(16)) s9 (.D(Write_Data), .en(and_10_out), .Q(s9_q), .clk(Register_CLOCK), .clr(Register_CLEAR));
  Register #(.width(16)) s10 (.D(Write_Data), .en(and_11_out), .Q(s10_q), .clk(Register_CLOCK), .clr(Register_CLEAR));
  Register #(.width(16)) s11 (.D(Write_Data), .en(and_12_out), .Q(s11_q), .clk(Register_CLOCK), .clr(Register_CLEAR));
  Register #(.width(16)) s12 (.D(Write_Data), .en(and_13_out), .Q(s12_q), .clk(Register_CLOCK), .clr(Register_CLEAR));
  Register #(.width(16)) s13 (.D(Write_Data), .en(and_14_out), .Q(s13_q), .clk(Register_CLOCK), .clr(Register_CLEAR));
  Register #(.width(16)) s14 (.D(Write_Data), .en(and_15_out), .Q(s14_q), .clk(Register_CLOCK), .clr(Register_CLEAR));
  Register #(.width(16)) s15 (.D(Write_Data), .en(and_16_out), .Q(s15_q), .clk(Register_CLOCK), .clr(Register_CLEAR));
  Multiplexer #(.select(4), .width(16), .enable("false")) multiplexer_1 (
    .in0(s0_q), .in1(s1_q), .in2(s2_q), .in3(s3_q), .in4(s4_q), .in5(s5_q), .in6(s6_q), .in7(s7_q),
    .in8(s8_q), .in9(s9_q), .in10(s10_q), .in11(s11_q), .in12(s12_q), .in13(s13_q), .in14(s14_q),
    .in15(s15_q), .out(Data_1_Out), .sel(RS_Selector));
  Multiplexer #(.select(4), .width(16), .enable("false")) multiplexer_2 (
    .in0(s0_q), .in1(s1_q), .in2(s2_q), .in3(s3_q), .in4(s4_q), .in5(s5_q), .in6(s6_q), .in7(s7_q),
    .in8(s8_q), .in9(s9_q), .in10(s10_q), .in11(s11_q), .in12(s12_q), .in13(s13_q), .in14(s14_q),
    .in15(s15_q), .out(Data_2_Out), .sel(RT_Selector));

  // Notes on the sheet:
  //   Md Ulfat Tahsin_1913057642
endmodule

module Md_Ulfat_Tahsin_1913057642_Lab_Task5 (
  input  [15:0] Write_Data,
  input  W_en,
  input  CLR,
  output [3:0] Opcode,
  output [3:0] RS,
  output [3:0] RT,
  output [3:0] RD,
  output [15:0] Data_1,
  output [15:0] Data_2
);

  wire Clock_out;
  wire [15:0] adder_1_out, register_1_q;

  Register #(.width(16)) register_1 (.D(adder_1_out), .Q(register_1_q), .clk(Clock_out));  // open: en, clr
  Clock Clock (.out(Clock_out));
  // Probe on Write_Data
  Adder #(.width(16)) adder_1 (.a(register_1_q), .b(16'h1), .out(adder_1_out));  // open: cin, cout
  ROM #(.addrWidth(16), .dataWidth(16)) rom_1 (.addr(register_1_q), .data({Opcode, RS, RT, RD}));  // open: sel
  _16_bit_register_file u_16_bit_register_file_1 (
    .Write_Data(Write_Data), .Write_enabler(W_en), .RT_Selector(RT), .RD_Selector(RD),
    .Register_CLOCK(Clock_out), .Data_1_Out(Data_1), .RS_Selector(RS), .Data_2_Out(Data_2),
    .Register_CLEAR(CLR));
  // Probe on Data_1
  // Probe on Data_2

  // Notes on the sheet:
  //   Instruction counter
  //   contents of rom_1 (hex, n*v repeats v):
  //   1234 2345 4444 5555 7777 101
  //   Md Ulfat Tahsin_1913057
  //   Data 1 shows output from RS
  //   Data 2 shows output from RT
endmodule

module ex (
  input  [15:0] Write_Data,
  input  [1:0] operation,
  input  Cin,
  input  W_en,
  input  CLR,
  input  [1:0] operation_2,
  input  Cin_2,
  input  a_invert,
  input  b_invert,
  input  a_invert_2,
  input  b_invert_2,
  output [3:0] Opcode,
  output [3:0] RS,
  output [3:0] RT,
  output [3:0] RD,
  output [15:0] Data_1,
  output [15:0] ALU_out,
  output [15:0] Data_2
);

  wire Clock_out;
  wire [15:0] adder_1_p3, register_1_q;

  Register #(.width(16)) register_1 (.D(adder_1_p3), .Q(register_1_q), .clk(Clock_out));  // open: en, clr
  Clock Clock (.out(Clock_out));
  // Probe on Write_Data
  // Adder #(.width(16)) adder_1: pin names not known; wires that end beside it: register_1_q, 16'h1, adder_1_p3
  ROM #(.addrWidth(16), .dataWidth(16)) rom_1 (.addr(register_1_q), .data({Opcode, RS, RT, RD}));  // open: sel
  _16_bit_register_file u_16_bit_register_file_1 (
    .Write_Data(ALU_out), .Write_enabler(W_en), .RT_Selector(RT), .RD_Selector(RD),
    .Register_CLOCK(Clock_out), .Data_1_Out(Data_1), .RS_Selector(RS), .Data_2_Out(Data_2),
    .Register_CLEAR(CLR));
  // Probe on Data_1
  // Probe on Data_2
  // Probe on ALU_out

  // Notes on the sheet:
  //   Instruction counter
  //   contents of rom_1 (hex, n*v repeats v):
  //   0 0 0 56f 1 108 100 102 13*0 100 200 2 1 1 110
  //   Md Ulfat Tahsin_1913057
  //   Data 1 shows output from RS
  //   Data 2 shows output from RT
endmodule

module _1_bit_adder (
  input  A1,
  input  B1,
  input  Carry_in,
  output SUM1,
  output Cout
);

  wire and_1_out, and_2_out, xor_1_out;

  xor xor_1 (xor_1_out, A1, B1);
  and and_1 (and_1_out, xor_1_out, Carry_in);
  and and_2 (and_2_out, A1, B1);
  xor xor_2 (SUM1, xor_1_out, Carry_in);
  or or_1 (Cout, and_1_out, and_2_out);
endmodule

module _2_1_bit_ALU (
  input  a,
  input  Ain,
  input  Cin_for_adder,
  input  b,
  input  [1:0] ALU_Op,
  input  Bin,
  output out_7,
  output out_8
);

  wire and_1_out, multiplexer_1_out, multiplexer_2_out, n1_bit_adder_1_sum1, not_1_out, not_2_out, or_1_out,
       xor_1_out;

  not not_1 (not_1_out, a);
  not not_2 (not_2_out, b);
  Multiplexer #(.enable("false")) multiplexer_1 (.in0(a), .in1(not_1_out), .out(multiplexer_1_out), .sel(Ain));
  Multiplexer #(.enable("false")) multiplexer_2 (.in0(b), .in1(not_2_out), .out(multiplexer_2_out), .sel(Bin));
  and and_1 (and_1_out, multiplexer_1_out, multiplexer_2_out);
  or or_1 (or_1_out, multiplexer_1_out, multiplexer_2_out);
  _1_bit_adder u_1_bit_adder_1 (
    .A1(multiplexer_1_out), .B1(multiplexer_2_out), .Carry_in(Cin_for_adder), .SUM1(n1_bit_adder_1_sum1),
    .Cout(out_8));
  xor xor_1 (xor_1_out, multiplexer_1_out, multiplexer_2_out);
  Multiplexer #(.select(2), .enable("false")) multiplexer_3 (
    .in0(and_1_out), .in1(or_1_out), .in2(n1_bit_adder_1_sum1), .in3(xor_1_out), .out(out_7), .sel(ALU_Op));
  // Probe on out_7
endmodule

module _2_16_bi_ALU (
  input  Cin,
  input  [15:0] a,
  input  [15:0] b,
  input  [1:0] Operation,
  input  Ain,
  input  Bin,
  output [15:0] S,
  output Zero_Signal,
  output out_9
);

  wire n2_1_bit_alu_1_out_8, n2_1_bit_alu_2_out_8, n2_1_bit_alu_3_out_8, n2_1_bit_alu_4_out_8,
       n2_1_bit_alu_5_out_8, n2_1_bit_alu_6_out_8, n2_1_bit_alu_7_out_8, n2_1_bit_alu_8_out_8,
       n2_1_bit_alu_9_out_8, n2_1_bit_alu_10_out_8, n2_1_bit_alu_11_out_8, n2_1_bit_alu_12_out_8,
       n2_1_bit_alu_13_out_8, n2_1_bit_alu_14_out_8, n2_1_bit_alu_15_out_8, n2_1_bit_alu_16_out_8;

  // Probe on a
  // Probe on b
  _2_1_bit_ALU u_2_1_bit_alu_1 (
    .a(a[0]), .Ain(Ain), .Cin_for_adder(Cin), .b(b[0]), .Bin(Bin), .out_7(S[0]),
    .out_8(n2_1_bit_alu_1_out_8), .ALU_Op(Operation));
  _2_1_bit_ALU u_2_1_bit_alu_2 (
    .a(a[1]), .Ain(Ain), .Cin_for_adder(n2_1_bit_alu_1_out_8), .b(b[1]), .Bin(Bin), .out_7(S[1]),
    .out_8(n2_1_bit_alu_2_out_8), .ALU_Op(Operation));
  _2_1_bit_ALU u_2_1_bit_alu_3 (
    .a(a[2]), .Ain(Ain), .Cin_for_adder(n2_1_bit_alu_2_out_8), .b(b[2]), .Bin(Bin), .out_7(S[2]),
    .out_8(n2_1_bit_alu_3_out_8), .ALU_Op(Operation));
  _2_1_bit_ALU u_2_1_bit_alu_4 (
    .a(a[3]), .Ain(Ain), .Cin_for_adder(n2_1_bit_alu_3_out_8), .b(b[3]), .Bin(Bin), .out_7(S[3]),
    .out_8(n2_1_bit_alu_4_out_8), .ALU_Op(Operation));
  // Probe on S
  _2_1_bit_ALU u_2_1_bit_alu_5 (
    .a(a[4]), .Ain(Ain), .Cin_for_adder(n2_1_bit_alu_4_out_8), .b(b[4]), .Bin(Bin), .out_7(S[4]),
    .out_8(n2_1_bit_alu_5_out_8), .ALU_Op(Operation));
  _2_1_bit_ALU u_2_1_bit_alu_6 (
    .a(a[5]), .Ain(Ain), .Cin_for_adder(n2_1_bit_alu_5_out_8), .b(b[5]), .Bin(Bin), .out_7(S[5]),
    .out_8(n2_1_bit_alu_6_out_8), .ALU_Op(Operation));
  _2_1_bit_ALU u_2_1_bit_alu_7 (
    .a(a[6]), .Ain(Ain), .Cin_for_adder(n2_1_bit_alu_6_out_8), .b(b[6]), .Bin(Bin), .out_7(S[6]),
    .out_8(n2_1_bit_alu_7_out_8), .ALU_Op(Operation));
  _2_1_bit_ALU u_2_1_bit_alu_8 (
    .a(a[7]), .Ain(Ain), .Cin_for_adder(n2_1_bit_alu_7_out_8), .b(b[7]), .Bin(Bin), .out_7(S[7]),
    .out_8(n2_1_bit_alu_8_out_8), .ALU_Op(Operation));
  _2_1_bit_ALU u_2_1_bit_alu_9 (
    .a(a[8]), .Ain(Ain), .Cin_for_adder(n2_1_bit_alu_8_out_8), .b(b[8]), .Bin(Bin), .out_7(S[8]),
    .out_8(n2_1_bit_alu_9_out_8), .ALU_Op(Operation));
  _2_1_bit_ALU u_2_1_bit_alu_10 (
    .a(a[9]), .Ain(Ain), .Cin_for_adder(n2_1_bit_alu_9_out_8), .b(b[9]), .Bin(Bin), .out_7(S[9]),
    .out_8(n2_1_bit_alu_10_out_8), .ALU_Op(Operation));
  _2_1_bit_ALU u_2_1_bit_alu_11 (
    .a(a[10]), .Ain(Ain), .Cin_for_adder(n2_1_bit_alu_10_out_8), .b(b[10]), .Bin(Bin), .out_7(S[10]),
    .out_8(n2_1_bit_alu_11_out_8), .ALU_Op(Operation));
  _2_1_bit_ALU u_2_1_bit_alu_12 (
    .a(a[11]), .Ain(Ain), .Cin_for_adder(n2_1_bit_alu_11_out_8), .b(b[11]), .Bin(Bin), .out_7(S[11]),
    .out_8(n2_1_bit_alu_12_out_8), .ALU_Op(Operation));
  _2_1_bit_ALU u_2_1_bit_alu_13 (
    .a(a[12]), .Ain(Ain), .Cin_for_adder(n2_1_bit_alu_12_out_8), .b(b[12]), .Bin(Bin), .out_7(S[12]),
    .out_8(n2_1_bit_alu_13_out_8), .ALU_Op(Operation));
  _2_1_bit_ALU u_2_1_bit_alu_14 (
    .a(a[13]), .Ain(Ain), .Cin_for_adder(n2_1_bit_alu_13_out_8), .b(b[13]), .Bin(Bin), .out_7(S[13]),
    .out_8(n2_1_bit_alu_14_out_8), .ALU_Op(Operation));
  _2_1_bit_ALU u_2_1_bit_alu_15 (
    .a(a[14]), .Ain(Ain), .Cin_for_adder(n2_1_bit_alu_14_out_8), .b(b[14]), .Bin(Bin), .out_7(S[14]),
    .out_8(n2_1_bit_alu_15_out_8), .ALU_Op(Operation));
  _2_1_bit_ALU u_2_1_bit_alu_16 (
    .a(a[15]), .Ain(Ain), .Cin_for_adder(n2_1_bit_alu_15_out_8), .b(b[15]), .Bin(Bin), .out_7(S[15]),
    .out_8(n2_1_bit_alu_16_out_8), .ALU_Op(Operation));
  xor xor_1 (out_9, n2_1_bit_alu_15_out_8, n2_1_bit_alu_16_out_8);
  nor u_Zero_SIgnal (Zero_Signal, S[0], S[1], S[2], S[3], S[4], S[5], S[6], S[7], S[8], S[9], S[10], S[11], S[12], S[13], S[14], S[15]);

  // Notes on the sheet:
  //   Zero Signal
endmodule

module R_type (
  input  [1:0] ALU_Opcode,
  input  Cin,
  input  [15:0] Write_Data,
  input  Ain,
  input  Bin,
  input  W_en,
  input  CLR,
  output [3:0] Opcode,
  output [3:0] RS,
  output [3:0] RT,
  output [3:0] RD,
  output [15:0] Data_1,
  output Beq_Zero_Signal,
  output [15:0] S,
  output Overflow1,
  output [15:0] Data_2
);

  wire Clock_out;
  wire [15:0] adder_1_out, register_1_q;

  Register #(.width(16)) register_1 (.D(adder_1_out), .Q(register_1_q), .clk(Clock_out));  // open: en, clr
  Clock Clock (.out(Clock_out));
  // Probe on Write_Data
  Adder #(.width(16)) adder_1 (.a(register_1_q), .b(16'h1), .out(adder_1_out));  // open: cin, cout
  ROM #(.addrWidth(16), .dataWidth(16)) rom_1 (.addr(register_1_q), .data({Opcode, RS, RT, RD}));  // open: sel
  _16_bit_register_file u_16_bit_register_file_1 (
    .Write_Data(S), .Write_enabler(W_en), .RT_Selector(RT), .RD_Selector(RD), .Register_CLOCK(Clock_out),
    .Data_1_Out(Data_1), .RS_Selector(RS), .Data_2_Out(Data_2), .Register_CLEAR(CLR));
  // Probe on Data_1
  // Probe on Data_2
  _2_16_bi_ALU u_2_16_bi_alu_1 (
    .a(Data_1), .b(Data_2), .Operation(ALU_Opcode), .Ain(Ain), .Bin(Bin), .S(S), .out_9(Overflow1),
    .Cin(Cin), .Zero_Signal(Beq_Zero_Signal));
  // Probe on S

  // Notes on the sheet:
  //   Instruction counter
  //   contents of rom_1 (hex, n*v repeats v):
  //   12 200 300 56f 1 108 100 102 8 8 8 110 f ff0
  //   Md Ulfat Tahsin_1913057
  //   Data 1 shows output from RS
  //   Data 2 shows output from RT
endmodule

module I_type (
  input  [1:0] ALU_opcode,
  input  Cin,
  input  [15:0] Write_Data,
  input  Ain,
  input  Bin,
  input  W_en,
  input  CLR,
  output [3:0] Opcode,
  output [3:0] RS,
  output [3:0] RT,
  output [3:0] RD,
  output [15:0] Data_1,
  output Beq_Zero_Signal,
  output [15:0] S,
  output Overflow1,
  output [15:0] Data_2
);

  wire Clock_out;
  wire [15:0] adder_1_out, register_1_q;

  Register #(.width(16)) register_1 (.D(adder_1_out), .Q(register_1_q), .clk(Clock_out));  // open: en, clr
  Clock Clock (.out(Clock_out));
  // Probe on Write_Data
  Adder #(.width(16)) adder_1 (.a(register_1_q), .b(16'h1), .out(adder_1_out));  // open: cin, cout
  ROM #(.addrWidth(16), .dataWidth(16)) rom_1 (.addr(register_1_q), .data({Opcode, RS, RT, RD}));  // open: sel
  assign Data_2 = {{12{1'b0}}, RD};  // Bit_Extender bit_extender_1
  _16_bit_register_file u_16_bit_register_file_1 (
    .Write_Data(S), .Write_enabler(W_en), .RD_Selector(RT), .Register_CLOCK(Clock_out), .Data_1_Out(Data_1),
    .RS_Selector(RS), .Register_CLEAR(CLR));  // open: RT_Selector, Data_2_Out
  // Probe on Data_1
  // Probe on Data_2
  _2_16_bi_ALU u_2_16_bi_alu_1 (
    .a(Data_1), .b(Data_2), .Operation(ALU_opcode), .Ain(Ain), .Bin(Bin), .S(S), .out_9(Overflow1),
    .Cin(Cin), .Zero_Signal(Beq_Zero_Signal));
  // Probe on S

  // Notes on the sheet:
  //   Instruction counter
  //   contents of rom_1 (hex, n*v repeats v):
  //   123 20 300 56f 1 108 100 102 8 8 8 110 f ff0
  //   Immediate for I-type
  //   Md Ulfat Tahsin_1913057
  //   Used for immediate type input to ALU
  //   Data 1 shows output from RS
  //   Data 2 shows output from RT
  //   Addi r1, r2, 3
endmodule

module J_type (
  input  [1:0] ALU_Opcode,
  input  Cin,
  input  [15:0] Write_Data,
  input  Ain,
  input  Bin,
  input  W_en,
  input  CLR,
  output [3:0] Opcode,
  output [3:0] RS,
  output [3:0] RT,
  output [3:0] RD,
  output [15:0] Data_1,
  output Beq_Zero_Signal,
  output [15:0] S,
  output Overflow1,
  output [15:0] Data_2
);

  wire Clock_out;
  wire [15:0] adder_1_out, register_1_q;

  Register #(.width(16)) register_1 (.D(adder_1_out), .Q(register_1_q), .clk(Clock_out));  // open: en, clr
  Clock Clock (.out(Clock_out));
  // Probe on Write_Data
  Adder #(.width(16)) adder_1 (.a(register_1_q), .b(16'h1), .out(adder_1_out));  // open: cin, cout
  ROM #(.addrWidth(16), .dataWidth(16)) rom_1 (.addr(register_1_q), .data({Opcode, RS, RT, RD}));  // open: sel
  _16_bit_register_file u_16_bit_register_file_1 (
    .Write_Data(S), .Write_enabler(W_en), .RT_Selector(RT), .RD_Selector(RD), .Register_CLOCK(Clock_out),
    .Data_1_Out(Data_1), .RS_Selector(RS), .Data_2_Out(Data_2), .Register_CLEAR(CLR));
  // Probe on Data_1
  // Probe on Data_2
  _2_16_bi_ALU u_2_16_bi_alu_1 (
    .a(Data_1), .b(Data_2), .Operation(ALU_Opcode), .Ain(Ain), .Bin(Bin), .S(S), .out_9(Overflow1),
    .Cin(Cin), .Zero_Signal(Beq_Zero_Signal));
  // Probe on S

  // Notes on the sheet:
  //   Unconditional jump type
  //   Instruction counter
  //   contents of rom_1 (hex, n*v repeats v):
  //   12 200 300 56f 1 108 100 102 8 8 8 110 f ff0
  //   Md Ulfat Tahsin_1913057
  //   Data 1 shows output from RS
  //   Data 2 shows output from RT
endmodule

module Load_Store_type (
  input  [1:0] ALU_Opcode,
  input  Cin,
  input  [15:0] Write_Data,
  input  RT_RD,
  input  Ain,
  input  Bin,
  input  W_en,
  input  CLR,
  input  Store,
  input  Load,
  output [3:0] Opcode,
  output [3:0] RS,
  output [3:0] RT,
  output [3:0] RD,
  output [15:0] Data_1,
  output Beq_Zero_Signal,
  output [15:0] S,
  output Overflow1,
  output [15:0] Data_2,
  output [15:0] Loaded_value
);

  wire Clock_out, or_1_out;
  wire [3:0] multiplexer_1_out;
  wire [15:0] adder_1_out, bit_extender_1_out, register_1_q;

  Register #(.width(16)) register_1 (.D(adder_1_out), .Q(register_1_q), .clk(Clock_out));  // open: en, clr
  Clock Clock (.out(Clock_out));
  // Probe on Write_Data
  Adder #(.width(16)) adder_1 (.a(register_1_q), .b(16'h1), .out(adder_1_out));  // open: cin, cout
  ROM #(.addrWidth(16), .dataWidth(16)) rom_1 (.addr(register_1_q), .data({Opcode, RS, RT, RD}));  // open: sel
  Multiplexer #(.width(4), .enable("false")) multiplexer_1 (.in0(RT), .in1(RD), .out(multiplexer_1_out), .sel(RT_RD));
  assign bit_extender_1_out = {{12{1'b0}}, RD};  // Bit_Extender bit_extender_1
  _16_bit_register_file u_16_bit_register_file_1 (
    .Write_Data(S), .Write_enabler(W_en), .RT_Selector(multiplexer_1_out), .RD_Selector(multiplexer_1_out),
    .Register_CLOCK(Clock_out), .Data_1_Out(Data_1), .RS_Selector(RS), .Data_2_Out(Data_2),
    .Register_CLEAR(CLR));
  // Probe on Data_1
  // Probe on Data_2
  _2_16_bi_ALU u_2_16_bi_alu_1 (
    .a(Data_1), .b(bit_extender_1_out), .Operation(ALU_Opcode), .Ain(Ain), .Bin(Bin), .S(S),
    .out_9(Overflow1), .Cin(Cin), .Zero_Signal(Beq_Zero_Signal));
  RAM #(.addrWidth(16), .dataWidth(16), .bus("separate")) ram_1 (
    .addr(S), .din(Data_2), .data(Loaded_value), .str(Store), .sel(or_1_out), .clk(Clock_out), .ld(Load));  // open: clr
  or or_1 (or_1_out, Load, Store);
  // Probe on S
  // Probe on Loaded_value

  // Notes on the sheet:
  //   Instruction counter
  //   contents of rom_1 (hex, n*v repeats v):
  //   123 501 300 56f 1 108 100 102 8 8 8 110 f ff0
  //   Used here to determine offset as immediate value
  //   Md Ulfat Tahsin_1913057
  //   A is used to access the location
  //   D is used to write any data when storing
  //   Data 1 shows output from RS
  //   Or gate used to enable the RAM only when the load/store is being executed
  //   Data 2 shows output from RT
endmodule

module Datapath_all_formats (
  input  [1:0] ALU_Opcode,
  input  Cin,
  input  Jump,
  input  Clear_PC,
  input  RD_RT,
  input  in_6,
  input  Ain,
  input  Bin,
  input  W_en,
  input  CLR,
  input  Store,
  input  Load,
  input  ALU_load_store_MUX,
  output [11:0] Jump_location,
  output [3:0] Opcode,
  output [3:0] RS,
  output [3:0] RT,
  output [3:0] RD_immediate,
  output [15:0] Data_1,
  output Beq_Zero_Signal,
  output [15:0] S,
  output Overflow1,
  output [15:0] Data_2,
  output [15:0] Loaded_data
);

  wire Clock_out, or_1_out;
  wire [3:0] multiplexer_2_out;
  wire [15:0] adder_1_out, adder_2_out, bit_extender_1_out, bit_extender_2_out, multiplexer_1_out,
       multiplexer_3_out, multiplexer_4_out, PC_q;

  Multiplexer #(.width(16), .enable("false")) multiplexer_1 (
    .in0(adder_1_out), .in1(adder_2_out), .out(multiplexer_1_out), .sel(Jump));
  Register #(.width(16)) PC (.D(multiplexer_1_out), .Q(PC_q), .clk(Clock_out), .clr(Clear_PC));  // open: en
  Clock Clock (.out(Clock_out));
  Adder #(.width(16)) adder_1 (.a(PC_q), .b(16'h1), .out(adder_1_out));  // open: cin, cout
  ROM #(.addrWidth(16), .dataWidth(16)) rom_1 (
    .addr(PC_q), .data({Opcode, Jump_location[7:4], Jump_location[11:8], Jump_location[3:0]}));  // open: sel
  Multiplexer #(.width(4), .enable("false")) multiplexer_2 (
    .in0(Jump_location[3:0]), .in1(Jump_location[11:8]), .out(multiplexer_2_out), .sel(RD_RT));
  assign bit_extender_1_out = {{12{1'b0}}, Jump_location[3:0]};  // Bit_Extender bit_extender_1
  // Probe on Jump_location
  assign bit_extender_2_out = {{4{1'b0}}, Jump_location};  // Bit_Extender bit_extender_2
  _16_bit_register_file u_16_bit_register_file_1 (
    .Write_Data(multiplexer_4_out), .Write_enabler(W_en), .RT_Selector(Jump_location[11:8]),
    .RD_Selector(multiplexer_2_out), .Register_CLOCK(Clock_out), .Data_1_Out(Data_1),
    .RS_Selector(Jump_location[7:4]), .Data_2_Out(Data_2), .Register_CLEAR(CLR));
  Adder #(.width(16)) adder_2 (.a(bit_extender_2_out), .b(adder_1_out), .out(adder_2_out));  // open: cin, cout
  // Probe on Data_1
  // Probe on Data_2
  Multiplexer #(.width(16), .enable("false")) multiplexer_3 (
    .in0(Data_2), .in1(bit_extender_1_out), .out(multiplexer_3_out), .sel(in_6));
  RAM #(.addrWidth(16), .dataWidth(16), .bus("separate")) ram_1 (
    .addr(S), .din(Data_2), .data(Loaded_data), .str(Store), .sel(or_1_out), .clk(Clock_out), .ld(Load));  // open: clr
  _2_16_bi_ALU u_2_16_bi_alu_1 (
    .a(Data_1), .b(multiplexer_3_out), .Operation(ALU_Opcode), .Ain(Ain), .Bin(Bin), .S(S),
    .out_9(Overflow1), .Cin(Cin), .Zero_Signal(Beq_Zero_Signal));
  or or_1 (or_1_out, Load, Store);
  // Probe on Loaded_data
  // Probe on S
  Multiplexer #(.width(16), .enable("false")) multiplexer_4 (
    .in0(S), .in1(Loaded_data), .out(multiplexer_4_out), .sel(ALU_load_store_MUX));
  _7_Segment_Display u_7_segment_display_1 ();  // open: g, f, a, b, e, d, c, dp

  assign RD_immediate = Jump_location[3:0];
  assign RS = Jump_location[7:4];
  assign RT = Jump_location[11:8];

  // Notes on the sheet:
  //   5) j 2
  //   Instructions:
  //   1) add $s1, $s2, $s3
  //   2) addi $s1, $s2, 4
  //   3) sw $s1, 2($s2)
  //   4) lw $s1, 2($s2)
  //   Rd, Rs, Rt = JUMP
  //   4
  //   MUX4 is ised to get the target location for jump instructions
  //   Instruction counter
  //   contents of rom_1 (hex, n*v repeats v):
  //   234 531 6212 6212 7212 3 0 0 0 a002 0 0 a001
  //   1
  //   Used here to determine offset as immediate value
  //   MUX1 used here to switch between R/I type
  //   A is used to access the location
  //   D is used to write any data when storing
  //   Data 1 shows output from RS
  //   2
  //   Data 2 shows output from RT
  //   Or gate used to enable the RAM only when the load/store is being executed
  //   Md Ulfat Tahsin_1913057
  //   3
  //   MUX3 here is used to either to choose the value directly from ALU or the effective address from RAM for lw/sw
endmodule

module branch_circuit (
  input  [1:0] ALU_Opcode,
  input  Cin,
  input  beq_control,
  input  Jump,
  input  Clear_PC,
  input  RD_RT,
  input  in_7,
  input  Ain,
  input  Bin,
  input  W_en,
  input  CLR,
  input  Store,
  input  Load,
  input  ALU_load_store_MUX,
  output [15:0] ALU_load_store_MUX_2,
  output [11:0] Jump_location,
  output [3:0] Opcode,
  output [3:0] RS,
  output [3:0] RT,
  output [3:0] RD_immediate,
  output [15:0] Data_1,
  output Beq_Zero_Signal,
  output [15:0] S,
  output Overflow1,
  output [15:0] Data_2,
  output [15:0] Loaded_data
);

  wire and_1_out, Clock_out, or_1_out;
  wire [3:0] multiplexer_2_out;
  wire [15:0] adder_1_out, adder_2_out, bit_extender_1_out, bit_extender_2_out, bit_extender_3_out,
       multiplexer_1_out, multiplexer_4_out, multiplexer_5_out, PC_q;

  Multiplexer #(.width(16), .enable("false")) multiplexer_1 (
    .in0(adder_1_out), .in1(ALU_load_store_MUX_2), .out(multiplexer_1_out), .sel(Jump));
  Register #(.width(16)) PC (.D(multiplexer_1_out), .Q(PC_q), .clk(Clock_out), .clr(Clear_PC));  // open: en
  Clock Clock (.out(Clock_out));
  Adder #(.width(16)) adder_1 (.a(PC_q), .b(16'h1), .out(adder_1_out));  // open: cin, cout
  ROM #(.addrWidth(16), .dataWidth(16)) rom_1 (
    .addr(PC_q), .data({Opcode, Jump_location[7:4], Jump_location[11:8], Jump_location[3:0]}));  // open: sel
  Multiplexer #(.width(4), .enable("false")) multiplexer_2 (
    .in0(Jump_location[3:0]), .in1(Jump_location[11:8]), .out(multiplexer_2_out), .sel(RD_RT));
  assign bit_extender_1_out = {{12{1'b0}}, Jump_location[3:0]};  // Bit_Extender bit_extender_1
  // Probe on Jump_location
  assign bit_extender_2_out = {{4{1'b0}}, Jump_location};  // Bit_Extender bit_extender_2
  _16_bit_register_file u_16_bit_register_file_1 (
    .Write_Data(multiplexer_5_out), .Write_enabler(W_en), .RT_Selector(Jump_location[11:8]),
    .RD_Selector(multiplexer_2_out), .Register_CLOCK(Clock_out), .Data_1_Out(Data_1),
    .RS_Selector(Jump_location[7:4]), .Data_2_Out(Data_2), .Register_CLEAR(CLR));
  Adder #(.width(16)) adder_2 (.a(bit_extender_2_out), .b(adder_1_out), .out(adder_2_out));  // open: cin, cout
  assign bit_extender_3_out = {{12{1'b0}}, Jump_location[3:0]};  // Bit_Extender bit_extender_3
  // Probe on Data_1
  // Probe on Data_2
  // Probe on ALU_load_store_MUX_2
  Multiplexer #(.width(16), .enable("false")) multiplexer_3 (
    .in0(bit_extender_2_out), .in1(adder_2_out), .out(ALU_load_store_MUX_2), .sel(and_1_out));
  Multiplexer #(.width(16), .enable("false")) multiplexer_4 (
    .in0(Data_2), .in1(bit_extender_1_out), .out(multiplexer_4_out), .sel(in_7));
  RAM #(.addrWidth(16), .dataWidth(16), .bus("separate")) ram_1 (
    .addr(S), .din(Data_2), .data(Loaded_data), .str(Store), .sel(or_1_out), .clk(Clock_out), .ld(Load));  // open: clr
  _2_16_bi_ALU u_2_16_bi_alu_1 (
    .a(Data_1), .b(multiplexer_4_out), .Operation(ALU_Opcode), .Ain(Ain), .Bin(Bin), .S(S),
    .out_9(Overflow1), .Cin(Cin), .Zero_Signal(Beq_Zero_Signal));
  or or_1 (or_1_out, Load, Store);
  // Probe on Loaded_data
  and and_1 (and_1_out, beq_control, Beq_Zero_Signal);
  // Probe on S
  Multiplexer #(.width(16), .enable("false")) multiplexer_5 (
    .in0(S), .in1(Loaded_data), .out(multiplexer_5_out), .sel(ALU_load_store_MUX));

  assign RD_immediate = Jump_location[3:0];
  assign RS = Jump_location[7:4];
  assign RT = Jump_location[11:8];

  // Notes on the sheet:
  //   Rd, Rs, Rt = JUMP
  //   4
  //   MUX4 is ised to get the target location for jump instructions
  //   Instruction counter
  //   contents of rom_1 (hex, n*v repeats v):
  //   5 5 6212 5 7212 3 0 3 0 3 0 0 a001
  //   1
  //   Used here to determine offset as immediate value
  //   MUX1 used here to switch between R/I type
  //   A is used to access the location
  //   D is used to write any data when storing
  //   Data 1 shows output from RS
  //   2
  //   Data 2 shows output from RT
  //   Or gate used to enable the RAM only when the load/store is being executed
  //   Md Ulfat Tahsin_1913057
  //   3
  //   MUX3 here is used to either to choose the value directly from ALU or the effective address from RAM for lw/sw
endmodule

module control_unit (
  input  op0,
  input  op1,
  input  op2,
  input  op3,
  output RDorRT,
  output Write_enabler,
  output RorI_type,
  output ALUop,
  output Aluop2,
  output Bin,
  output lw,
  output sw,
  output RAM_enabler,
  output Result_memory_or_ALU,
  output beq,
  output jump
);

  wire and_1_out, and_2_out, and_3_out, and_4_out, and_5_out, and_6_out, and_11_out, and_12_out, and_14_out,
       and_15_out, and_16_out, not_1_out, not_2_out, not_3_out, not_4_out, not_5_out, not_6_out, not_7_out,
       not_8_out, not_9_out, not_10_out, not_11_out, not_12_out, not_13_out, not_14_out, not_15_out,
       not_16_out, not_17_out, not_18_out, not_19_out, not_20_out, not_21_out;

  and and_1 (and_1_out, op1, op2);
  and and_2 (and_2_out, op0, not_1_out);
  not not_1 (not_1_out, op2);
  and and_3 (and_3_out, op0, not_2_out);
  not not_2 (not_2_out, op3);
  not not_3 (not_3_out, op2);
  or or_1 (Write_enabler, not_3_out, op3, op1);
  or or_2 (RorI_type, op2, op0);
  not not_4 (not_4_out, op0);
  and and_4 (and_4_out, not_4_out, not_5_out);
  not not_5 (not_5_out, op1);
  and and_5 (and_5_out, op2, not_6_out);
  not not_6 (not_6_out, op3);
  and and_6 (and_6_out, op1, op2);
  not not_7 (not_7_out, op2);
  and and_7 (Aluop2, op1, not_7_out, op3);
  not not_8 (not_8_out, op0);
  not not_9 (not_9_out, op1);
  not not_10 (not_10_out, op2);
  not not_11 (not_11_out, op3);
  not not_12 (not_12_out, op0);
  not not_13 (not_13_out, op1);
  not not_14 (not_14_out, op3);
  not not_15 (not_15_out, op1);
  and and_8 (sw, not_15_out, op2, op3);
  not not_16 (not_16_out, op0);
  and and_9 (RAM_enabler, not_16_out, not_17_out, op2);
  not not_17 (not_17_out, op1);
  not not_18 (not_18_out, op0);
  and and_10 (Result_memory_or_ALU, not_18_out, not_19_out, op2);
  not not_19 (not_19_out, op1);
  and and_11 (and_11_out, op0, not_20_out, op2);
  not not_20 (not_20_out, op1);
  and and_12 (and_12_out, op0, op2, not_21_out);
  not not_21 (not_21_out, op3);
  and and_13 (jump, op0, op2);
  or or_3 (RDorRT, and_1_out, and_2_out, and_3_out);
  or or_4 (ALUop, and_4_out, and_5_out, and_6_out);
  and and_14 (and_14_out, not_8_out, not_9_out, not_10_out, op3);
  and and_15 (and_15_out, op1, op2, op3);
  or or_5 (Bin, and_14_out, and_15_out, and_16_out);
  and and_16 (and_16_out, op0, op2, not_11_out);
  and and_17 (lw, not_12_out, not_13_out, op2, not_14_out);
  or or_6 (beq, and_11_out, and_12_out);
endmodule

module cu (
  input  Clear_PC,
  input  Ain,
  input  CLR,
  output [11:0] Jump_location,
  output [3:0] Opcode,
  output [3:0] RS,
  output Data_1,
  output [3:0] RT,
  output [1:0] ALUop,
  output [3:0] RD_immediate,
  output [15:0] Data_1_2,
  output Beq_Zero_Signal,
  output [15:0] S,
  output Overflow1,
  output RD_RT,
  output write_enabler,
  output [15:0] Data_2,
  output [15:0] Loaded_data,
  output Load,
  output Store,
  output ALU_load_store_MUX
);

  wire beq_control_out, Clock_out, control_unit_1_beq, control_unit_1_jump, control_unit_1_ram_enabler,
       control_unit_1_rori_type;
  wire [3:0] multiplexer_2_out;
  wire [15:0] adder_1_out, adder_2_out, bit_extender_1_out, bit_extender_2_out, multiplexer_1_out,
       multiplexer_3_out, multiplexer_4_out, multiplexer_5_out, PC_q;

  Multiplexer #(.width(16), .enable("false")) multiplexer_1 (
    .in0(adder_1_out), .in1(multiplexer_3_out), .out(multiplexer_1_out), .sel(control_unit_1_jump));
  Register #(.width(16)) PC (.D(multiplexer_1_out), .Q(PC_q), .clk(Clock_out), .clr(Clear_PC));  // open: en
  Clock Clock (.out(Clock_out));
  Adder #(.width(16)) adder_1 (.a(PC_q), .b(16'h1), .out(adder_1_out));  // open: cin, cout
  ROM #(.addrWidth(16), .dataWidth(16)) rom_1 (
    .addr(PC_q), .data({Opcode, Jump_location[7:4], Jump_location[11:8], Jump_location[3:0]}));  // open: sel
  control_unit control_unit_1 (
    .op0(Opcode[3]), .op1(Opcode[2]), .RDorRT(RD_RT), .op2(Opcode[1]), .op3(Opcode[0]),
    .Write_enabler(write_enabler), .RorI_type(control_unit_1_rori_type), .ALUop(ALUop[1]), .Aluop2(ALUop[0]),
    .Bin(Data_1), .lw(Load), .sw(Store), .RAM_enabler(control_unit_1_ram_enabler),
    .Result_memory_or_ALU(ALU_load_store_MUX), .beq(control_unit_1_beq), .jump(control_unit_1_jump));
  Multiplexer #(.width(4), .enable("false")) multiplexer_2 (
    .in0(Jump_location[3:0]), .in1(Jump_location[11:8]), .out(multiplexer_2_out), .sel(RD_RT));
  assign bit_extender_1_out = {{12{1'b0}}, Jump_location[3:0]};  // Bit_Extender bit_extender_1
  // Probe on Jump_location
  assign bit_extender_2_out = {{4{1'b0}}, Jump_location};  // Bit_Extender bit_extender_2
  _16_bit_register_file u_16_bit_register_file_1 (
    .Write_Data(multiplexer_5_out), .Write_enabler(write_enabler), .RT_Selector(Jump_location[11:8]),
    .RD_Selector(multiplexer_2_out), .Register_CLOCK(Clock_out), .Data_1_Out(Data_1_2),
    .RS_Selector(Jump_location[7:4]), .Data_2_Out(Data_2), .Register_CLEAR(CLR));
  Adder #(.width(16)) adder_2 (.a(bit_extender_2_out), .b(adder_1_out), .out(adder_2_out));  // open: cin, cout
  // Probe on Data_1_2
  // Probe on Data_2
  Multiplexer #(.width(16), .enable("false")) multiplexer_3 (
    .in0(adder_1_out), .in1(adder_2_out), .out(multiplexer_3_out), .sel(beq_control_out));
  Multiplexer #(.width(16), .enable("false")) multiplexer_4 (
    .in0(Data_2), .in1(bit_extender_1_out), .out(multiplexer_4_out), .sel(control_unit_1_rori_type));
  RAM #(.addrWidth(16), .dataWidth(16), .bus("separate")) ram_1 (
    .addr(S), .din(Data_2), .data(Loaded_data), .str(Store), .sel(control_unit_1_ram_enabler),
    .clk(Clock_out), .ld(Load));  // open: clr
  _2_16_bi_ALU u_2_16_bi_alu_1 (
    .a(Data_1_2), .b(multiplexer_4_out), .Operation(ALUop), .Ain(Ain), .Bin(Data_1), .S(S),
    .out_9(Overflow1), .Cin(Data_1), .Zero_Signal(Beq_Zero_Signal));
  // Probe on Loaded_data
  and beq_control (beq_control_out, control_unit_1_beq, Beq_Zero_Signal);
  // Probe on S
  Multiplexer #(.width(16), .enable("false")) multiplexer_5 (
    .in0(S), .in1(Loaded_data), .out(multiplexer_5_out), .sel(ALU_load_store_MUX));

  assign RD_immediate = Jump_location[3:0];
  assign RS = Jump_location[7:4];
  assign RT = Jump_location[11:8];

  // Notes on the sheet:
  //   Rd, Rs, Rt = JUMP
  //   4
  //   MUX4 is ised to get the target location for jump instructions
  //   Instruction counter
  //   contents of rom_1 (hex, n*v repeats v):
  //   3023 3023 6212 5 7212 2000 0 0 0 3 0 0 a001
  //   1
  //   Used here to determine offset as immediate value
  //   MUX1 used here to switch between R/I type
  //   A is used to access the location
  //   D is used to write any data when storing
  //   Data 1 shows output from RS
  //   2
  //   Data 2 shows output from RT
  //   Or gate used to enable the RAM only when the load/store is being executed
  //   Md Ulfat Tahsin_1913057
  //   3
  //   MUX3 here is used to either to choose the value directly from ALU or the effective address from RAM for lw/sw
endmodule

module a (
);

  wire dd2_1_a_2, dd2_1_b_2, dd2_1_c, dd2_1_d, dd2_1_e, dd2_1_f, dd2_1_g, dd_1_a_2, dd_1_b_2, dd_1_c_2,
       dd_1_d_2, dd_1_e, dd_1_f, dd_1_g, dd_2_a_2, dd_2_b_2, dd_2_c_2, dd_2_d_2, dd_2_e, dd_2_f, dd_2_g,
       dd_3_a_2, dd_3_b_2, dd_3_c_2, dd_3_d_2, dd_3_e, dd_3_f, dd_3_g;
  wire [13:0] shanto_q;

  Register #(.width(14)) shanto (.Q(shanto_q));  // open: D, en, clk, clr
  dd2 dd2_1 (
    .A(shanto_q[13]), .B(shanto_q[12]), .a_2(dd2_1_a_2), .b_2(dd2_1_b_2), .c(dd2_1_c), .d(dd2_1_d),
    .e(dd2_1_e), .f(dd2_1_f), .g(dd2_1_g));
  _7_Segment_Display u_7_segment_display_1 (
    .g(dd2_1_g), .f(dd2_1_f), .a(dd2_1_a_2), .b(dd2_1_b_2), .e(dd2_1_e), .d(dd2_1_d), .c(dd2_1_c));  // open: dp
  dd dd_1 (
    .A(shanto_q[11]), .B(shanto_q[10]), .C(shanto_q[9]), .D(shanto_q[8]), .a_2(dd_1_a_2), .b_2(dd_1_b_2),
    .c_2(dd_1_c_2), .d_2(dd_1_d_2), .e(dd_1_e), .f(dd_1_f), .g(dd_1_g));
  _7_Segment_Display u_7_segment_display_2 (
    .g(dd_1_g), .f(dd_1_f), .a(dd_1_a_2), .b(dd_1_b_2), .e(dd_1_e), .d(dd_1_d_2), .c(dd_1_c_2));  // open: dp
  dd dd_2 (
    .A(shanto_q[3]), .B(shanto_q[2]), .C(shanto_q[1]), .D(shanto_q[0]), .a_2(dd_2_a_2), .b_2(dd_2_b_2),
    .c_2(dd_2_c_2), .d_2(dd_2_d_2), .e(dd_2_e), .f(dd_2_f), .g(dd_2_g));
  dd dd_3 (
    .A(shanto_q[7]), .B(shanto_q[6]), .C(shanto_q[5]), .D(shanto_q[4]), .a_2(dd_3_a_2), .b_2(dd_3_b_2),
    .c_2(dd_3_c_2), .d_2(dd_3_d_2), .e(dd_3_e), .f(dd_3_f), .g(dd_3_g));
  _7_Segment_Display u_7_segment_display_3 (
    .g(dd_2_g), .f(dd_2_f), .a(dd_2_a_2), .b(dd_2_b_2), .e(dd_2_e), .d(dd_2_d_2), .c(dd_2_c_2));  // open: dp
  _7_Segment_Display u_7_segment_display_4 (
    .g(dd_3_g), .f(dd_3_f), .a(dd_3_a_2), .b(dd_3_b_2), .e(dd_3_e), .d(dd_3_d_2), .c(dd_3_c_2));  // open: dp
endmodule

module dd (
  input  A,
  input  B,
  input  C,
  input  D,
  output a_2,
  output b_2,
  output c_2,
  output d_2,
  output e,
  output f,
  output g
);

  wire and_1_out, and_2_out, and_3_out, and_4_out, and_5_out, and_6_out, and_7_out, and_8_out, and_9_out,
       and_10_out, and_11_out, and_12_out, and_13_out, and_14_out, and_15_out, and_16_out, and_17_out,
       and_18_out, and_19_out, and_20_out, and_21_out, and_22_out, and_23_out, and_24_out, and_25_out,
       and_26_out, and_27_out, and_28_out, and_29_out, and_30_out, and_31_out, and_32_out, and_33_out,
       not_1_out, not_2_out, not_3_out, not_4_out, not_5_out, not_6_out, not_7_out, not_8_out, not_9_out,
       not_10_out, not_11_out, not_12_out, not_13_out, not_14_out, not_15_out, not_16_out, not_17_out,
       not_18_out, not_19_out, not_20_out, not_21_out, not_22_out, not_23_out, not_24_out, not_25_out,
       not_26_out, not_27_out, not_28_out, not_29_out, not_30_out, not_31_out, not_32_out, not_33_out,
       not_34_out, not_35_out, not_36_out, not_37_out, not_38_out, not_39_out, not_40_out, not_41_out,
       not_42_out;

  not not_1 (not_1_out, A);
  not not_2 (not_2_out, B);
  and and_1 (and_1_out, not_1_out, not_2_out, not_3_out);
  not not_3 (not_3_out, D);
  not not_4 (not_4_out, A);
  and and_2 (and_2_out, not_4_out, C);
  not not_5 (not_5_out, A);
  and and_3 (and_3_out, not_5_out, B, D);
  and and_4 (and_4_out, B, C);
  and and_5 (and_5_out, A, not_6_out, not_7_out);
  not not_6 (not_6_out, B);
  not not_7 (not_7_out, C);
  not not_8 (not_8_out, A);
  not not_9 (not_9_out, B);
  not not_10 (not_10_out, A);
  not not_11 (not_11_out, C);
  not not_12 (not_12_out, D);
  not not_13 (not_13_out, B);
  not not_14 (not_14_out, C);
  not not_15 (not_15_out, A);
  not not_16 (not_16_out, C);
  not not_17 (not_17_out, D);
  not not_18 (not_18_out, A);
  and and_6 (and_6_out, not_18_out, not_19_out);
  not not_19 (not_19_out, C);
  not not_20 (not_20_out, A);
  and and_7 (and_7_out, not_20_out, D);
  not not_21 (not_21_out, C);
  and and_8 (and_8_out, not_21_out, D);
  not not_22 (not_22_out, A);
  and and_9 (and_9_out, not_22_out, B);
  and and_10 (and_10_out, A, not_23_out);
  not not_23 (not_23_out, B);
  not not_24 (not_24_out, B);
  and and_11 (and_11_out, not_24_out, not_25_out);
  not not_25 (not_25_out, D);
  not not_26 (not_26_out, B);
  and and_12 (and_12_out, not_26_out, C);
  and and_13 (and_13_out, C, not_27_out);
  not not_27 (not_27_out, D);
  not not_28 (not_28_out, C);
  and and_14 (and_14_out, B, not_28_out, D);
  and and_15 (and_15_out, A, not_29_out);
  not not_29 (not_29_out, C);
  not not_30 (not_30_out, B);
  and and_16 (and_16_out, not_30_out, not_31_out);
  not not_31 (not_31_out, D);
  and and_17 (and_17_out, C, not_32_out);
  not not_32 (not_32_out, D);
  and and_18 (and_18_out, A, C);
  and and_19 (and_19_out, A, B);
  not not_33 (not_33_out, B);
  not not_34 (not_34_out, C);
  and and_20 (and_20_out, not_33_out, not_34_out, not_35_out);
  not not_35 (not_35_out, D);
  not not_36 (not_36_out, A);
  and and_21 (and_21_out, not_36_out, B, not_37_out);
  not not_37 (not_37_out, C);
  and and_22 (and_22_out, B, C, not_38_out);
  not not_38 (not_38_out, D);
  and and_23 (and_23_out, A, not_39_out, D);
  not not_39 (not_39_out, B);
  and and_24 (and_24_out, A, B, C);
  not not_40 (not_40_out, B);
  and and_25 (and_25_out, not_40_out, C);
  and and_26 (and_26_out, B, not_41_out);
  not not_41 (not_41_out, C);
  and and_27 (and_27_out, B, not_42_out);
  not not_42 (not_42_out, D);
  or or_1 (a_2, and_1_out, and_2_out, and_3_out, and_4_out, and_5_out);
  and and_28 (and_28_out, not_8_out, not_9_out);
  and and_29 (and_29_out, not_10_out, not_11_out, not_12_out);
  and and_30 (and_30_out, not_13_out, not_14_out);
  and and_31 (and_31_out, not_15_out, C, D);
  and and_32 (and_32_out, A, not_16_out, D);
  and and_33 (and_33_out, A, B, C, not_17_out);
  or or_2 (c_2, and_6_out, and_7_out, and_8_out, and_9_out, and_10_out);
  or or_3 (d_2, and_11_out, and_12_out, and_13_out, and_14_out, and_15_out);
  or or_4 (e, and_16_out, and_17_out, and_18_out, and_19_out);
  or or_5 (f, and_20_out, and_21_out, and_22_out, and_23_out, and_24_out);
  or or_6 (g, and_25_out, and_26_out, and_27_out, A);
  or or_7 (b_2, and_28_out, and_29_out, and_30_out, and_31_out, and_32_out, and_33_out);
endmodule

module dd2 (
  input  A,
  input  B,
  output a_2,
  output b_2,
  output c,
  output d,
  output e,
  output f,
  output g
);

  wire not_1_out, not_2_out, not_3_out, not_5_out, not_6_out;

  not not_1 (not_1_out, B);
  not not_2 (not_2_out, A);
  not not_3 (not_3_out, B);
  not not_4 (e, B);
  not not_5 (not_5_out, A);
  not not_6 (not_6_out, B);
  or or_1 (a_2, not_1_out, A);
  or or_2 (c, not_2_out, B);
  or or_3 (d, not_3_out, A);
  and and_1 (f, not_5_out, not_6_out);

  assign b_2 = 1'b1;
  assign g = A;
endmodule
